// Logisim project ALU.circ as structural Verilog: 1 circuit, main circuit ALU
module ALU (
  input  in_1,
  input  in_2,
  input  [3:0] in_3,
  input  [31:0] in_4,
  input  [31:0] in_5,
  output out_6,
  output out_7,
  output out_8,
  output [31:0] out_9,
  output [31:0] out_10,
  output [31:0] out_11
);

  wire comparator_1_lt, comparator_2_lt;
  wire [1:0] SELECTOR_MULT_DIV;
  wire [31:0] ADD, AND, multiplexer_2_out, multiplexer_3_out, MUX_1_1, MUX_1_2, MUX_1_3, MUX_1_4, MUX_2_1,
       MUX_2_2, MUX_2_3, MUX_2_4, NOR, OR, SLT, SLTU, SUB, XOR;

  Signed_Multipler signed_multipler_1 (.in_1(in_4), .in_2(in_5), .out_3(MUX_2_1), .out_4(MUX_1_1));
  Signed_Divider signed_divider_1 (.in_1(in_4), .in_2(in_5), .out_3(MUX_2_3), .out_4(MUX_1_3));
  assign AND = in_4 & in_5;  // AND_Gate and_1, 32 bits wide
  assign OR = in_4 | in_5;  // OR_Gate or_1, 32 bits wide
  assign NOR = ~(in_4 | in_5);  // NOR_Gate nor_1, 32 bits wide
  assign XOR = in_4 ^ in_5;  // XOR_Gate xor_1, 32 bits wide
  Comparator #(.width(32)) comparator_1 (.a(in_4), .b(in_5), .eq(out_8), .lt(comparator_1_lt));  // open: gt
  Comparator #(.width(32)) comparator_2 (.a(in_4), .b(in_5), .lt(comparator_2_lt));  // open: gt, eq
  Adder #(.width(32)) adder_1 (.a(in_4), .b(in_5), .out(ADD));  // open: cin, cout
  Subtractor #(.width(32)) subtractor_1 (.a(in_4), .b(in_5), .out(SUB));  // open: bin, bout
  Multiplier #(.width(32)) multiplier_1 (.a(in_4), .b(in_5), .out(MUX_2_2), .cout(MUX_1_2));  // open: cin
  Divider #(.width(32)) divider_1 (.a(in_4), .b(in_5), .out(MUX_2_4), .rem(MUX_1_4));  // open: upper
  assign SLT = {{31{1'b0}}, comparator_1_lt};  // Bit_Extender bit_extender_1
  assign SLTU = {{31{1'b0}}, comparator_2_lt};  // Bit_Extender bit_extender_2
  and and_2 (SELECTOR_MULT_DIV[0], in_3[3], ~in_3[2], in_3[0]);  // AND_Gate
  and and_3 (SELECTOR_MULT_DIV[1], in_3[1], ~in_3[2], in_3[3]);  // AND_Gate
  Comparator #(.width(32)) comparator_3 (.a(in_4), .b({32{1'b0}}), .eq(out_6), .lt(out_7));  // open: gt
  Multiplexer #(.select(4), .width(32), .enable("false")) multiplexer_1 (
    .in0(AND), .in1(OR), .in2(NOR), .in3(XOR), .in4(SLT), .in5(SLTU), .in6(ADD), .in7(SUB), .out(out_9),
    .sel(in_3));  // open: in8, in9, in10, in11, in12, in13, in14, in15
  Multiplexer #(.select(2), .width(32), .enable("false")) multiplexer_2 (
    .in0(MUX_1_1), .in1(MUX_1_2), .in2(MUX_1_3), .in3(MUX_1_4), .out(multiplexer_2_out),
    .sel(SELECTOR_MULT_DIV));
  Multiplexer #(.select(2), .width(32), .enable("false")) multiplexer_3 (
    .in0(MUX_2_1), .in1(MUX_2_2), .in2(MUX_2_3), .in3(MUX_2_4), .out(multiplexer_3_out),
    .sel(SELECTOR_MULT_DIV));
  Register #(.width(32)) register_1 (.D(multiplexer_2_out), .en(in_2), .clk(in_1));  // open: Q, clr
  Register #(.width(32)) register_2 (.D(multiplexer_3_out), .en(in_2), .Q(out_11), .clk(in_1));  // open: clr

  // Other names for the same wires on the sheet: A[31:0] = in_4; ALU_SELECTOR[3:0] = in_3; B[31:0] = in_5; CLK = in_1;
  //   ENABLE_HIGH_LOW = in_2; EQF = out_8; HIGH[31:0] = out_10; LOW[31:0] = out_11; Output[31:0] = out_9

  // Notes on the sheet:
  //   INPUTS
  //   OUTPUTS
  //   ALU
endmodule
