// Logisim project Branch Control.circ as structural Verilog: 1 circuit, main circuit Branch Control
module Branch_Control (
  input  [31:0] Inputs,
  input  [15:0] in_2,
  input  [25:0] in_3,
  input  [31:0] in_4,
  input  [1:0] in_5,
  output [31:0] Output
);

  wire [1:0] BS;
  wire [15:0] multiplier_1_out, Offset;
  wire [25:0] Destination;
  wire [27:0] PC;
  wire [31:0] bit_extender_1_out, PC_4, PC_4__Offser_4, PC_star;
  wire [31:28] Jump;

  Adder #(.width(32)) adder_1 (.a({Jump, PC}), .b(32'h4), .out(PC_4));  // open: cin, cout
  assign bit_extender_1_out = {{16{multiplier_1_out[15]}}, multiplier_1_out};  // Bit_Extender bit_extender_1
  Multiplier #(.width(16)) multiplier_1 (.a(Offset), .b(16'h4), .out(multiplier_1_out));  // open: cin, cout
  Multiplexer #(.select(2), .width(32), .enable("false")) multiplexer_1 (
    .in0(PC_4), .in1(PC_4__Offser_4), .in3({Jump, Destination, 2'b00}), .out(PC_star), .sel(BS));  // open: in2
  Adder #(.width(32)) adder_2 (.a(PC_4), .b(bit_extender_1_out), .out(PC_4__Offser_4));  // open: cin, cout

  // Other names for the same wires on the sheet: Jump[27:2] = Destination; PC[31:28] = Jump

  // Notes on the sheet:
  //   Branch Control
endmodule
