// Logisim project Instruction Decoder.circ as structural Verilog: 1 circuit, main circuit Instruction Decoder
module Instruction_Decoder (
  input  [5:0] in_1,
  input  [25:0] in_2,
  input  [4:0] in_3,
  input  [31:0] Instruction,
  input  [4:0] in_5,
  input  [15:0] in_6,
  input  [4:0] in_7,
  input  [5:0] in_8
);


  assign in_3 = in_2[25:21];
  assign in_5 = in_2[20:16];
  assign in_6 = in_2[15:0];
  assign in_7 = in_2[15:11];
  assign in_8 = in_2[5:0];
  assign Instruction = {in_1, in_2};

  // Other names for the same wires on the sheet: Const[15:0] = in_2[15:0]; Destination_Jump[25:0] = in_2;
  //   Func_Code[5:0] = in_2[5:0]; Rd[4:0] = in_2[15:11]; Rt[4:0] = in_2[20:16]; Rs[4:0] = in_2[25:21];
  //   Op_Code[5:0] = in_1

  // Notes on the sheet:
  //   Instruction Decoder
  //   OutPuts
endmodule
