// Logisim project Signed Divider.circ as structural Verilog: 1 circuit, main circuit Signed Divider
module Signed_Divider (
  input  [31:0] in_1,
  input  [31:0] in_2,
  output [31:0] out_3,
  output [31:0] out_4
);

  wire xor_1_out;
  wire [31:0] divider_1_out, In_Div1, In_Div2, negator_1_out, negator_2_out, negator_3_out;

  // Probe on in_1
  // Probe on in_2
  Divider #(.width(32)) divider_1 (.a(In_Div1), .b(In_Div2), .out(divider_1_out), .rem(out_4));  // open: upper
  // Probe on out_4
  Negator #(.width(32)) negator_1 (.in(in_1), .out(negator_1_out));
  Negator #(.width(32)) negator_2 (.in(in_2), .out(negator_2_out));
  xor xor_1 (xor_1_out, in_1[31], in_2[31]);
  Negator #(.width(32)) negator_3 (.in(divider_1_out), .out(negator_3_out));
  Multiplexer #(.width(32), .enable("false")) multiplexer_1 (
    .in0(in_1), .in1(negator_1_out), .out(In_Div1), .sel(in_1[31]));
  Multiplexer #(.width(32), .enable("false")) multiplexer_2 (
    .in0(in_2), .in1(negator_2_out), .out(In_Div2), .sel(in_2[31]));
  // Probe on out_3
  Multiplexer #(.width(32), .enable("false")) multiplexer_3 (
    .in0(divider_1_out), .in1(negator_3_out), .out(out_3), .sel(xor_1_out));

  // Other names for the same wires on the sheet: Carry_Out[31:0] = out_4; Input1[31:0] = in_1; Sign1 = in_1[31];
  //   Input2[31:0] = in_2; Sign2 = in_2[31]; Result[31:0] = out_3

  // Notes on the sheet:
  //   INPUT
  //   OUTPUT
  //   Part1
  //   Part2
  //   Separador
  //   Separador
endmodule
