// Logisim project Signed Multipler.circ as structural Verilog: 1 circuit, main circuit Signed Multipler
module Signed_Multipler (
  input  [31:0] in_1,
  input  [31:0] in_2,
  output [31:0] out_3,
  output [31:0] out_4
);

  wire adder_1_cout, SIGN;
  wire [31:0] adder_1_out, adder_2_out, In_Mult1, In_Mult2, multiplier_1_cout, multiplier_1_out,
       negator_1_out, negator_2_out, not_1_out, not_2_out;

  // Probe on in_1
  // Probe on in_2
  Multiplier #(.width(32)) multiplier_1 (
    .a(In_Mult1), .b(In_Mult2), .out(multiplier_1_out), .cout(multiplier_1_cout));  // open: cin
  Negator #(.width(32)) negator_1 (.in(in_1), .out(negator_1_out));
  Negator #(.width(32)) negator_2 (.in(in_2), .out(negator_2_out));
  assign not_1_out = ~multiplier_1_out;  // NOT_Gate not_1, 32 bits wide
  assign not_2_out = ~multiplier_1_cout;  // NOT_Gate not_2, 32 bits wide
  Multiplexer #(.width(32), .enable("false")) multiplexer_1 (
    .in0(in_1), .in1(negator_1_out), .out(In_Mult1), .sel(in_1[31]));
  Multiplexer #(.width(32), .enable("false")) multiplexer_2 (
    .in0(in_2), .in1(negator_2_out), .out(In_Mult2), .sel(in_2[31]));
  Adder #(.width(32)) adder_1 (.a(not_1_out), .b(32'h1), .out(adder_1_out), .cout(adder_1_cout));  // open: cin
  Adder #(.width(32)) adder_2 (.a(not_2_out), .b({32{1'b0}}), .out(adder_2_out), .cin(adder_1_cout));  // open: cout
  // Probe on out_3
  Multiplexer #(.width(32), .enable("false")) multiplexer_3 (
    .in0(multiplier_1_out), .in1(adder_1_out), .out(out_3), .sel(SIGN));
  Multiplexer #(.width(32), .enable("false")) multiplexer_4 (
    .in0(multiplier_1_cout), .in1(adder_2_out), .out(out_4), .sel(SIGN));
  // Probe on out_4
  xor xor_1 (SIGN, in_1[31], in_2[31]);

  // Other names for the same wires on the sheet: Carry_Out[31:0] = out_4; Input1[31:0] = in_1; Sign1 = in_1[31];
  //   Input2[31:0] = in_2; Sign2 = in_2[31]; Result[31:0] = out_3

  // Notes on the sheet:
  //   INPUT
  //   OUTPUT
  //   Part1
  //   Part2
  //   Separador
  //   Separador
  //   SIGN
endmodule
