// Logisim project PC.circ as structural Verilog: 1 circuit, main circuit PC
module PC (
  input  [31:0] PC_in,
  input  Enable,
  input  CLK,
  input  Reset,
  output [31:0] PC_out
);

  Register #(.width(32)) PC (.D(PC_in), .en(Enable), .Q(PC_out), .clk(CLK), .clr(Reset));

  // Notes on the sheet:
  //   Program Counter
endmodule
