// Logisim project Register Bank.circ as structural Verilog: 1 circuit, main circuit Register Bank
module Register_Bank (
  input  in_1,
  input  in_2,
  input  in_3,
  input  [4:0] in_4,
  input  [4:0] in_5,
  input  [4:0] in_6,
  input  [31:0] in_7,
  output [31:0] out_8,
  output [31:0] out_9,
  output [31:0] out_10
);

  wire Input_0, Input_1, Input_2, Input_3, Input_4, Input_5, Input_6, Input_7, Input_8, Input_9, Input_10,
       Input_11, Input_12, Input_13, Input_14, Input_15, Input_16, Input_17, Input_18, Input_19, Input_20,
       Input_21, Input_22, Input_23, Input_24, Input_25, Input_26, Input_27, Input_28, Input_29, Input_30,
       Input_31;
  wire [31:0] R0, R1, R2, R3, R4, R5, R6, R7, R8, R9, R10, R11, R12, R13, R14, R15, R16, R17, R18, R19, R20,
       R21, R22, R23, R24, R25, R26, R27, R28, R29, R30;

  Demultiplexer #(.select(5), .enable("false")) demultiplexer_1 (
    .out0(Input_0), .out1(Input_1), .out2(Input_2), .out3(Input_3), .out4(Input_4), .out5(Input_5),
    .out6(Input_6), .out7(Input_7), .out8(Input_8), .out9(Input_9), .out10(Input_10), .out11(Input_11),
    .out12(Input_12), .out13(Input_13), .out14(Input_14), .out15(Input_15), .out16(Input_16),
    .out17(Input_17), .out18(Input_18), .out19(Input_19), .out20(Input_20), .out21(Input_21),
    .out22(Input_22), .out23(Input_23), .out24(Input_24), .out25(Input_25), .out26(Input_26),
    .out27(Input_27), .out28(Input_28), .out29(Input_29), .out30(Input_30), .out31(Input_31), .in(in_3),
    .sel(in_6));
  Multiplexer #(.select(5), .width(32), .enable("false")) multiplexer_1 (
    .in0(R0), .in1(R1), .in2(R2), .in3(R3), .in4(R4), .in5(R5), .in6(R6), .in7(R7), .in8(R8), .in9(R9),
    .in10(R10), .in11(R11), .in12(R12), .in13(R13), .in14(R14), .in15(R15), .in16(R16), .in17(R17),
    .in18(R18), .in19(R19), .in20(R20), .in21(R21), .in22(R22), .in23(R23), .in24(R24), .in25(R25),
    .in26(R26), .in27(R27), .in28(R28), .in29(R29), .in30(R30), .in31(out_10), .out(out_8), .sel(in_4));
  Register #(.width(32)) u_R0 (.D({32{1'b0}}), .en(Input_0), .Q(R0), .clk(in_1), .clr(in_2));
  Register #(.width(32)) u_R1 (.D(in_7), .en(Input_1), .Q(R1), .clk(in_1), .clr(in_2));
  Register #(.width(32)) u_R2 (.D(in_7), .en(Input_2), .Q(R2), .clk(in_1), .clr(in_2));
  Register #(.width(32)) u_R3 (.D(in_7), .en(Input_3), .Q(R3), .clk(in_1), .clr(in_2));
  Register #(.width(32)) u_R4 (.D(in_7), .en(Input_4), .Q(R4), .clk(in_1), .clr(in_2));
  Register #(.width(32)) u_R5 (.D(in_7), .en(Input_5), .Q(R5), .clk(in_1), .clr(in_2));
  Register #(.width(32)) u_R6 (.D(in_7), .en(Input_6), .Q(R6), .clk(in_1), .clr(in_2));
  Register #(.width(32)) u_R7 (.D(in_7), .en(Input_7), .Q(R7), .clk(in_1), .clr(in_2));
  Register #(.width(32)) u_R8 (.D(in_7), .en(Input_8), .Q(R8), .clk(in_1), .clr(in_2));
  Register #(.width(32)) u_R9 (.D(in_7), .en(Input_9), .Q(R9), .clk(in_1), .clr(in_2));
  Register #(.width(32)) u_R10 (.D(in_7), .en(Input_10), .Q(R10), .clk(in_1), .clr(in_2));
  Register #(.width(32)) u_R11 (.D(in_7), .en(Input_11), .Q(R11), .clk(in_1), .clr(in_2));
  Register #(.width(32)) u_R12 (.D(in_7), .en(Input_12), .Q(R12), .clk(in_1), .clr(in_2));
  Register #(.width(32)) u_R13 (.D(in_7), .en(Input_13), .Q(R13), .clk(in_1), .clr(in_2));
  Register #(.width(32)) u_R14 (.D(in_7), .en(Input_14), .Q(R14), .clk(in_1), .clr(in_2));
  Register #(.width(32)) u_R15 (.D(in_7), .en(Input_15), .Q(R15), .clk(in_1), .clr(in_2));
  Multiplexer #(.select(5), .width(32), .enable("false")) multiplexer_2 (
    .in0(R0), .in1(R1), .in2(R2), .in3(R3), .in4(R4), .in5(R5), .in6(R6), .in7(R7), .in8(R8), .in9(R9),
    .in10(R10), .in11(R11), .in12(R12), .in13(R13), .in14(R14), .in15(R15), .in16(R16), .in17(R17),
    .in18(R18), .in19(R19), .in20(R20), .in21(R21), .in22(R22), .in23(R23), .in24(R24), .in25(R25),
    .in26(R26), .in27(R27), .in28(R28), .in29(R29), .in30(R30), .in31(out_10), .out(out_9), .sel(in_5));
  Register #(.width(32)) u_R16 (.D(in_7), .en(Input_16), .Q(R16), .clk(in_1), .clr(in_2));
  Register #(.width(32)) u_R17 (.D(in_7), .en(Input_17), .Q(R17), .clk(in_1), .clr(in_2));
  Register #(.width(32)) u_R18 (.D(in_7), .en(Input_18), .Q(R18), .clk(in_1), .clr(in_2));
  Register #(.width(32)) u_R19 (.D(in_7), .en(Input_19), .Q(R19), .clk(in_1), .clr(in_2));
  Register #(.width(32)) u_R20 (.D(in_7), .en(Input_20), .Q(R20), .clk(in_1), .clr(in_2));
  Register #(.width(32)) u_R21 (.D(in_7), .en(Input_21), .Q(R21), .clk(in_1), .clr(in_2));
  Register #(.width(32)) u_R22 (.D(in_7), .en(Input_22), .Q(R22), .clk(in_1), .clr(in_2));
  Register #(.width(32)) u_R23 (.D(in_7), .en(Input_23), .Q(R23), .clk(in_1), .clr(in_2));
  Register #(.width(32)) u_R24 (.D(in_7), .en(Input_24), .Q(R24), .clk(in_1), .clr(in_2));
  Register #(.width(32)) u_R25 (.D(in_7), .en(Input_25), .Q(R25), .clk(in_1), .clr(in_2));
  Register #(.width(32)) u_R26 (.D(in_7), .en(Input_26), .Q(R26), .clk(in_1), .clr(in_2));
  Register #(.width(32)) u_R27 (.D(in_7), .en(Input_27), .Q(R27), .clk(in_1), .clr(in_2));
  Register #(.width(32)) u_R28 (.D(in_7), .en(Input_28), .Q(R28), .clk(in_1), .clr(in_2));
  Register #(.width(32)) u_R29 (.D(in_7), .en(Input_29), .Q(R29), .clk(in_1), .clr(in_2));
  Register #(.width(32)) u_R30 (.D(in_7), .en(Input_30), .Q(R30), .clk(in_1), .clr(in_2));
  Register #(.width(32)) R31 (.D(in_7), .en(Input_31), .Q(out_10), .clk(in_1), .clr(in_2));

  // Other names for the same wires on the sheet: CLK = in_1; DATA[31:0] = in_7; Destination[4:0] = in_6;
  //   Output_1[31:0] = out_8; Output_2[31:0] = out_9; ReadWrite = in_3; Reset = in_2; Selector_1[4:0] = in_4;
  //   Selector_2[4:0] = in_5; R31[31:0] = out_10; SP[31:0] = out_10

  // Notes on the sheet:
  //   Inputs
  //   Outputs
  //   Registers
endmodule
