// Logisim project s-mips.circ as structural Verilog: 19 circuits, main circuit S-MIPS Board
module S_MIPS_Board (
  input  DESHABILITAR_DISPATCHER,
  output halt
);

  wire button_1_out, CLK, CS, d_ff_1_q, LCLR, LoadRAM, LoadRAMOn, LW, R_R_W, R_W, ram_dispatcher_1_finished,
       RCS, Reset_out, RST, TTY_EN;
  wire [2:0] KDB;
  wire [3:0] LMask, Mask, ram_1_read_time, ram_1_write_time, RMask;
  wire [6:0] KDB_DATA, TTY_DATA;
  wire [15:0] Addr, LAddr, RAddr;
  wire [31:0] I0, I1, I2, I3, LData, ram_1_data_out_0, ram_1_data_out_1, ram_1_data_out_2, ram_1_data_out_3,
       RI0, RI1, RI2, RI3;

  TTY #(.rows(25), .cols(80)) tty_1 (.data(TTY_DATA), .clk(CLK), .we(TTY_EN), .clr(RST));
  not not_1 (LoadRAMOn, ram_dispatcher_1_finished);
  RAM_Dispatcher ram_dispatcher_1 (
    .WriteTime(ram_1_write_time), .Clock(CLK), .Data(LData), .Address(LAddr), .Mask(LMask),
    .Finished(ram_dispatcher_1_finished), .Write(LW), .CLR(LCLR));
  Keyboard #(.buflen(64)) keyboard_1 (.clk(CLK), .re(KDB[0]), .avail(KDB[2]), .data(KDB_DATA));  // open: clr
  RAM ram_1 (
    .Address(RAddr), .Data_Out_0(ram_1_data_out_0), .Data_Out_1(ram_1_data_out_1),
    .Data_Out_2(ram_1_data_out_2), .Data_Out_3(ram_1_data_out_3), .Data_In_0(RI0), .Data_In_1(RI1),
    .Data_In_2(RI2), .Data_In_3(RI3), .Mask(RMask), .nRead_Write(R_R_W), .Chip_Select(RCS),
    .Read_Time(ram_1_read_time), .Reset(button_1_out), .Write_Time(ram_1_write_time));
  Button button_1 (.out(button_1_out));
  D_Flip_Flop d_ff_1 (.clk(CLK), .D(1'b1), .Q(d_ff_1_q), .reset(Reset_out));  // open: Qn, preset, en
  Button Reset (.out(Reset_out));
  S_MIPS s_mips_1 (
    .Kbd_Enable(KDB[0]), .Address(Addr), .Kbd_Clear(KDB[1]), .Kbd_Available(KDB[2]), .RAM_In_0(I0),
    .Kbd_ASCII_Data(KDB_DATA), .RAM_In_1(I1), .TTY_Enable(TTY_EN), .RAM_In_2(I2), .RAM_In_3(I3),
    .TTY_ASCII_Data(TTY_DATA), .Reset(RST), .RAM_Out_0(ram_1_data_out_0), .Clock(CLK),
    .RAM_Out_1(ram_1_data_out_1), .Stop(halt), .RAM_Out_2(ram_1_data_out_2), .RAM_Out_3(ram_1_data_out_3),
    .Mask(Mask), .Read_Time(ram_1_read_time), .Write_Time(ram_1_write_time), .nRead_Write(R_W),
    .Chip_Select(CS));
  D_Flip_Flop d_ff_2 (.clk(CLK), .D(d_ff_1_q), .Qn(LCLR), .reset(Reset_out));  // open: Q, preset, en
  or or_1 (RST, LCLR, LoadRAM);
  Clock clock_1 (.out(CLK));
  Multiplexer #(.width(32), .enable("false")) multiplexer_1 (.in0(I0), .in1(LData), .out(RI0), .sel(LoadRAM));
  Multiplexer #(.width(32), .enable("false")) multiplexer_2 (.in0(I1), .in1(LData), .out(RI1), .sel(LoadRAM));
  Multiplexer #(.width(32), .enable("false")) multiplexer_3 (.in0(I2), .in1(LData), .out(RI2), .sel(LoadRAM));
  Multiplexer #(.width(32), .enable("false")) multiplexer_4 (.in0(I3), .in1(LData), .out(RI3), .sel(LoadRAM));
  and and_1 (LoadRAM, ~DESHABILITAR_DISPATCHER, LoadRAMOn);  // AND_Gate
  Multiplexer #(.width(16), .enable("false")) multiplexer_5 (.in0(Addr), .in1(LAddr), .out(RAddr), .sel(LoadRAM));
  Multiplexer #(.width(4), .enable("false")) multiplexer_6 (.in0(Mask), .in1(LMask), .out(RMask), .sel(LoadRAM));
  Multiplexer #(.enable("false")) multiplexer_7 (.in0(CS), .in1(LW), .out(RCS), .sel(LoadRAM));
  Multiplexer #(.enable("false")) multiplexer_8 (.in0(R_W), .in1(LW), .out(R_R_W), .sel(LoadRAM));

  // Notes on the sheet:
  //   NO MODIFICAR
  //   Keyboard
endmodule

module RAM (
  input  [15:0] Address,
  input  [31:0] Data_In_0,
  input  [31:0] Data_In_1,
  input  [31:0] Data_In_2,
  input  [31:0] Data_In_3,
  input  [3:0] Mask,
  input  nRead_Write,
  input  Chip_Select,
  input  Reset,
  output [31:0] Data_Out_0,
  output [31:0] Data_Out_1,
  output [31:0] Data_Out_2,
  output [31:0] Data_Out_3,
  output [3:0] Read_Time,
  output [3:0] Write_Time
);

  wire and_2_out, and_3_out, and_4_out, and_5_out, and_6_out, and_7_out, and_8_out, and_9_out, Changed, CLK,
       comparator_2_eq, comparator_3_eq, comparator_4_eq, comparator_5_eq, comparator_6_eq, Count,
       demultiplexer_3_out0, Idle, Idle_q, Load, Load0, Load1, nand_1_out, or_1_out, or_2_out, or_3_out,
       or_4_out, or_5_out, or_6_out, or_7_out, or_8_out, or_9_out, or_10_out, Proc_q, Update_Mem, Zero_Time;
  wire [3:0] counter_1_q, multiplexer_1_out, subtractor_1_out;
  wire [31:0] register_1_q, register_2_q, register_3_q, register_4_q, register_5_q;

  // Probe on 4'b0011
  // Probe on 4'b0010
  Multiplexer #(.width(4), .enable("false")) multiplexer_1 (
    .in0(4'b0011), .in1(4'b0010), .out(multiplexer_1_out), .sel(nRead_Write));
  or or_1 (or_1_out, Idle, Update_Mem);
  or or_2 (or_2_out, ~Chip_Select, Reset);  // OR_Gate
  Subtractor #(.width(4)) subtractor_1 (.a(multiplexer_1_out), .b(4'b0010), .out(subtractor_1_out));  // open: bin, bout
  Demultiplexer #(.enable("false")) demultiplexer_1 (.out0(Idle), .out1(Load0), .in(Idle_q), .sel(Changed));
  D_Flip_Flop u_Idle (.clk(CLK), .D(or_1_out), .Q(Idle_q), .preset(or_2_out));  // open: Qn, en, reset
  // Probe on counter_1_q
  Counter #(.width(4), .max('hf)) counter_1 (
    .load(Load), .D(subtractor_1_out), .count(Count), .Q(counter_1_q), .clk(CLK), .clr(or_3_out));  // open: carry
  or or_3 (or_3_out, ~Chip_Select, Reset);  // OR_Gate
  Comparator #(.width(4), .mode("unsigned")) comparator_1 (
    .a(4'b0000), .b(counter_1_q), .eq(Zero_Time));  // open: gt, lt
  or or_4 (or_4_out, Count, Load0, Load1);
  Register #(.width(32)) register_1 (.D(Data_In_0), .en(Chip_Select), .Q(register_1_q), .clk(CLK), .clr(or_5_out));
  or or_5 (or_5_out, ~Chip_Select, Reset);  // OR_Gate
  Register #(.width(32)) register_2 (.D(Data_In_1), .en(Chip_Select), .Q(register_2_q), .clk(CLK), .clr(or_6_out));
  or or_6 (or_6_out, ~Chip_Select, Reset);  // OR_Gate
  Register #(.width(32)) register_3 (.D(Data_In_2), .en(Chip_Select), .Q(register_3_q), .clk(CLK), .clr(or_7_out));
  or or_7 (or_7_out, ~Chip_Select, Reset);  // OR_Gate
  Register #(.width(32)) register_4 (.D(Data_In_3), .en(Chip_Select), .Q(register_4_q), .clk(CLK), .clr(or_8_out));
  or or_8 (or_8_out, ~Chip_Select, Reset);  // OR_Gate
  Register #(.width(32)) register_5 (
    .D({{11{1'b1}}, nRead_Write, Mask, Address}), .en(Chip_Select), .Q(register_5_q), .clk(CLK),
    .clr(or_9_out));
  or or_9 (or_9_out, ~Chip_Select, Reset);  // OR_Gate
  D_Flip_Flop Proc (.clk(CLK), .D(or_4_out), .Q(Proc_q), .reset(or_10_out));  // open: Qn, preset, en
  or or_10 (or_10_out, ~Chip_Select, Reset);  // OR_Gate
  Demultiplexer #(.enable("false")) demultiplexer_2 (
    .out0(Count), .out1(Update_Mem), .in(demultiplexer_3_out0), .sel(Zero_Time));
  Demultiplexer #(.enable("false")) demultiplexer_3 (
    .out0(demultiplexer_3_out0), .out1(Load1), .in(Proc_q), .sel(Changed));
  Clock clock_1 (.out(CLK));
  Comparator #(.width(32)) comparator_2 (.a(register_1_q), .b(Data_In_0), .eq(comparator_2_eq));  // open: gt, lt
  Comparator #(.width(32)) comparator_3 (.a(register_2_q), .b(Data_In_1), .eq(comparator_3_eq));  // open: gt, lt
  Comparator #(.width(32)) comparator_4 (.a(register_3_q), .b(Data_In_2), .eq(comparator_4_eq));  // open: gt, lt
  Comparator #(.width(32)) comparator_5 (.a(register_4_q), .b(Data_In_3), .eq(comparator_5_eq));  // open: gt, lt
  Comparator #(.width(32)) comparator_6 (
    .a(register_5_q), .b({{11{1'b1}}, nRead_Write, Mask, Address}), .eq(comparator_6_eq));  // open: gt, lt
  nand nand_1 (nand_1_out, comparator_6_eq, comparator_2_eq, comparator_3_eq, comparator_4_eq, comparator_5_eq);
  and and_1 (Changed, nand_1_out, Chip_Select);
  or or_11 (Load, Count, Load1, Load0);
  and and_2 (and_2_out, Mask[0], Update_Mem, nRead_Write);
  and and_3 (and_3_out, Mask[1], Update_Mem, nRead_Write);
  and and_4 (and_4_out, Mask[2], Update_Mem, nRead_Write);
  and and_5 (and_5_out, Mask[3], Update_Mem, nRead_Write);
  RAM_part #(.addrWidth(16), .dataWidth(32), .bus("separate")) ram_1 (
    .addr(Address), .din(Data_In_0), .data(Data_Out_0), .str(and_2_out), .sel(Chip_Select), .clk(CLK),
    .ld(and_6_out), .clr(Reset));
  and and_6 (and_6_out, ~nRead_Write, Idle);  // AND_Gate
  RAM_part #(.addrWidth(16), .dataWidth(32), .bus("separate")) ram_2 (
    .addr(Address), .din(Data_In_1), .data(Data_Out_1), .str(and_3_out), .sel(Chip_Select), .clk(CLK),
    .ld(and_7_out), .clr(Reset));
  and and_7 (and_7_out, ~nRead_Write, Idle);  // AND_Gate
  RAM_part #(.addrWidth(16), .dataWidth(32), .bus("separate")) ram_3 (
    .addr(Address), .din(Data_In_2), .data(Data_Out_2), .str(and_4_out), .sel(Chip_Select), .clk(CLK),
    .ld(and_8_out), .clr(Reset));
  and and_8 (and_8_out, ~nRead_Write, Idle);  // AND_Gate
  RAM_part #(.addrWidth(16), .dataWidth(32), .bus("separate")) ram_4 (
    .addr(Address), .din(Data_In_3), .data(Data_Out_3), .str(and_5_out), .sel(Chip_Select), .clk(CLK),
    .ld(and_9_out), .clr(Reset));
  and and_9 (and_9_out, ~nRead_Write, Idle);  // AND_Gate

  assign Read_Time = 4'b0011;
  assign Write_Time = 4'b0010;

  // Other names for the same wires on the sheet: M0 = Mask[0]; M1 = Mask[1]; M2 = Mask[2]; M3 = Mask[3];
  //   RW = nRead_Write; CLR = Reset; CS = Chip_Select; Load2 = Count

  // Notes on the sheet:
  //   NO MODIFICAR
  //   excepto quizás los valores RT y WT
  //   BANK0
  //   BANK1
  //   BANK2
  //   BANK3
endmodule

module S_MIPS (
  input  Kbd_Available,
  input  [6:0] Kbd_ASCII_Data,
  input  [31:0] RAM_Out_0,
  input  [31:0] RAM_Out_1,
  input  Reset,
  input  [31:0] RAM_Out_2,
  input  Clock,
  input  [31:0] RAM_Out_3,
  input  [3:0] Read_Time,
  input  [3:0] Write_Time,
  output Kbd_Enable,
  output [15:0] Address,
  output Kbd_Clear,
  output TTY_Enable,
  output [6:0] TTY_ASCII_Data,
  output Stop,
  output [31:0] RAM_In_0,
  output [31:0] RAM_In_1,
  output [31:0] RAM_In_2,
  output [31:0] RAM_In_3,
  output [3:0] Mask,
  output nRead_Write,
  output Chip_Select
);

  wire ALU_SRC_A, EQF, EXTEND_SLC, HI_LOW_LOAD, IN_EN, NF, PC_EN, R_W, RESULT_LOAD, VALUE_SRC, ZF;
  wire [1:0] ADR_SRC, ALU_SRC_B, BC_SLC, DA_SLC;
  wire [2:0] DATA_SLC;
  wire [3:0] ALU_CONTROL;
  wire [5:0] Func_Code, Op_Code;
  wire [31:0] DATA, MEMORY, VALUE;

  READ_RAM read_ram_1 (
    .in_1(RAM_Out_0), .in_2(MEMORY), .in_3(RAM_Out_1), .in_4(RAM_Out_2), .in_5(RAM_Out_3), .RAM_DATA(DATA));
  WRITE_RAM write_ram_1 (
    .VALOR(VALUE), .MEMORIA(MEMORY), .INPUT1(RAM_In_0), .MASK(Mask), .INPUT2(RAM_In_1), .INPUT3(RAM_In_2),
    .INPUT4(RAM_In_3), .ADDRESS(Address));
  UNIT_CONTROL unit_control_1 (
    .Output(ALU_SRC_A), .Output_2(R_W), .out_12(nRead_Write), .Output_3(ALU_SRC_B), .Output_4(PC_EN),
    .out_15(Chip_Select), .Output_5(ADR_SRC), .Output_6(TTY_Enable), .out_18(HI_LOW_LOAD), .Output_7(BC_SLC),
    .Output_8(Stop), .Output_9(DA_SLC), .Output_10(VALUE_SRC), .Output_11(DATA_SLC), .Output_12(Kbd_Enable),
    .Output_13(ALU_CONTROL), .Output_14(IN_EN), .Output_15(EXTEND_SLC), .Output_16(RESULT_LOAD),
    .in_1(Clock), .in_2(Reset), .ENTRADAS(ZF), .in_4(NF), .in_5(EQF), .in_6(Op_Code), .in_7(Func_Code),
    .in_8(Read_Time), .in_9(Write_Time));
  DATA_PATH data_path_1 (
    .in_4(BC_SLC), .in_1(Clock), .in_6(DA_SLC), .in_3(Reset), .in_2(ALU_SRC_B), .in_5(IN_EN),
    .in_8(DATA_SLC), .in_7(R_W), .in_11(ALU_CONTROL), .in_10(RESULT_LOAD), .in_13(Kbd_ASCII_Data),
    .in_12(HI_LOW_LOAD), .in_14(Kbd_Available), .in_15(DATA), .in_17(PC_EN), .in_18(EXTEND_SLC),
    .in_19(ALU_SRC_A), .Address(MEMORY), .Value(VALUE), .TTY_DATA(TTY_ASCII_Data), .Op_Code(Op_Code),
    .Func_Code(Func_Code), .Address_Selector(ADR_SRC), .Value_Selector(VALUE_SRC), .out_25(EQF), .out_26(NF),
    .out_27(ZF));

  assign Kbd_Clear = Reset;

  // Other names for the same wires on the sheet: CLK = Clock; CS = Chip_Select; KBD_AVAIL = Kbd_Available;
  //   CLR = Reset; KBD_CLR = Reset; KBD_DATA[6:0] = Kbd_ASCII_Data; RAM_A[15:0] = Address;
  //   RAM_INPUT_0[31:0] = RAM_In_0; RAM_INPUT_1[31:0] = RAM_In_1; RAM_INPUT_2[31:0] = RAM_In_2;
  //   RAM_INPUT_3[31:0] = RAM_In_3; RAM_MASK[3:0] = Mask; RAM_OUTPUT_0[31:0] = RAM_Out_0;
  //   RAM_OUTPUT_1[31:0] = RAM_Out_1; RAM_OUTPUT_2[31:0] = RAM_Out_2; RAM_OUTPUT_3[31:0] = RAM_Out_3;
  //   RW = nRead_Write; TTY_DATA[6:0] = TTY_ASCII_Data

  // Notes on the sheet:
  //   RAM ADDRESS
  //   DATA FROM RAM
  //   DATA TO RAM
  //   DATA WRITE MASK
  //   RAM TIMING
  //   RAM CONTROL
  //   KEYBOARD
  //   TTY
  //   SEQUENCING
endmodule

module RAM_Dispatcher (
  input  [3:0] WriteTime,
  input  Clock,
  input  CLR,
  output [31:0] Data,
  output [15:0] Address,
  output [3:0] Mask,
  output Finished,
  output Write
);

  wire demultiplexer_2_out1, demultiplexer_3_out1, End, IDLE_q, IncAddr, Load, or_1_out, or_2_out, While_q,
       WriteEnd;
  wire [3:0] counter_1_q;
  wire [31:0] CurrentAddress_q;

  Counter #(.width(32), .max('hffffffff)) CurrentAddress (
    .count(IncAddr), .Q({CurrentAddress_q[31:18], Address, CurrentAddress_q[1:0]}), .clk(Clock), .clr(CLR));  // open: load, D, carry
  or or_1 (or_1_out, IncAddr, demultiplexer_3_out1, Finished);
  D_Flip_Flop IDLE (.clk(Clock), .D(or_1_out), .Q(IDLE_q), .preset(CLR));  // open: Qn, en, reset
  Demultiplexer #(.enable("false")) demultiplexer_1 (.out0(Load), .out1(Finished), .in(IDLE_q), .sel(End));
  D_Flip_Flop While (.clk(Clock), .D(or_2_out), .Q(While_q), .reset(CLR));  // open: Qn, preset, en
  or or_2 (or_2_out, Write, Load);
  RAM_part #(.addrWidth(18), .dataWidth(32)) ram_1 (
    .addr({Address, CurrentAddress_q[1:0]}), .data(Data), .clk(Clock));  // open: sel, ld, clr
  Demultiplexer #(.enable("false")) demultiplexer_2 (
    .out0(Write), .out1(demultiplexer_2_out1), .in(While_q), .sel(WriteEnd));
  Decoder #(.select(2)) decoder_1 (
    .out0(Mask[0]), .out1(Mask[1]), .out2(Mask[2]), .out3(Mask[3]), .sel(CurrentAddress_q[1:0]));  // open: en
  Demultiplexer #(.enable("false")) demultiplexer_3 (
    .out0(IncAddr), .out1(demultiplexer_3_out1), .in(demultiplexer_2_out1), .sel(End));
  Counter #(.width(4), .max('hf)) counter_1 (
    .load(Load), .D(WriteTime), .count(Write), .Q(counter_1_q), .clk(Clock));  // open: carry, clr
  Comparator #(.width(32)) comparator_1 (.a(Data), .b({32{1'b1}}), .eq(End));  // open: gt, lt
  Comparator #(.width(4)) comparator_2 (.a(4'b0000), .b(counter_1_q), .eq(WriteEnd));  // open: gt, lt

  // Other names for the same wires on the sheet: CLK = Clock; Count = Write; WT[3:0] = WriteTime
endmodule

module DATA_PATH (
  input  in_1,
  input  [1:0] in_2,
  input  in_3,
  input  [1:0] in_4,
  input  in_5,
  input  [1:0] in_6,
  input  in_7,
  input  [2:0] in_8,
  input  [1:0] Address_Selector,
  input  in_10,
  input  [3:0] in_11,
  input  in_12,
  input  [6:0] in_13,
  input  in_14,
  input  [31:0] in_15,
  input  Value_Selector,
  input  in_17,
  input  in_18,
  input  in_19,
  output [31:0] Address,
  output [31:0] Value,
  output [6:0] TTY_DATA,
  output [5:0] Op_Code,
  output [5:0] Func_Code,
  output out_25,
  output out_26,
  output out_27
);

  wire [4:0] multiplexer_7_out, Rd, Rs, Rt;
  wire [15:0] Constante;
  wire [25:0] Destination_Jump;
  wire [31:0] ALU, alu_1_out_9, bit_extender_1_out, bit_extender_2_out, bit_extender_3_out,
       branch_control_1_out_6, Data, Hi, KBD, Lo, multiplexer_2_out, multiplexer_3_out, multiplexer_4_out,
       multiplexer_8_out, PC, R_2_q, Random_Generator, RT_t, Sp;
  wire [31:7] RS_t;

  Random #(.width(32)) random_1 (.clk(in_1), .next(in_1), .out(Random_Generator));  // open: clr
  Register #(.width(32)) R (.D(in_15), .en(in_1), .Q(Data), .clk(in_1), .clr(in_3));
  assign bit_extender_1_out = {{25{1'b0}}, in_13};  // Bit_Extender bit_extender_1
  Register #(.width(32), .trigger("falling")) R_2 (.D(in_15), .en(in_5), .Q(R_2_q), .clk(in_1), .clr(in_3));
  Multiplexer #(.width(32), .enable("false")) multiplexer_1 (
    .in0({32{1'b1}}), .in1(bit_extender_1_out), .out(KBD), .sel(in_14));
  Branch_Control branch_control_1 (
    .in_1(PC), .in_2(Constante), .in_3(Destination_Jump), .in_4({RS_t, TTY_DATA}), .in_5(in_4),
    .out_6(branch_control_1_out_6));
  Instruction_Decoder instruction_decoder_1 (
    .out_2(Op_Code), .out_3(Destination_Jump), .out_4(Rs), .out_5(Rt), .out_6(Constante), .out_7(Rd),
    .out_8(Func_Code), .in_1(R_2_q));
  PC pc_1 (.PC_in(branch_control_1_out_6), .Enable(in_17), .CLK(in_1), .Reset(in_3), .PC_out(PC));
  assign bit_extender_2_out = {{16{Constante[15]}}, Constante};  // Bit_Extender bit_extender_2
  assign bit_extender_3_out = {{16{1'b0}}, Constante};  // Bit_Extender bit_extender_3
  Multiplexer #(.width(32), .enable("false")) multiplexer_2 (
    .in0(bit_extender_2_out), .in1(bit_extender_3_out), .out(multiplexer_2_out), .sel(in_18));
  Multiplexer #(.width(32), .enable("false")) multiplexer_3 (
    .in0({RS_t, TTY_DATA}), .in1(Sp), .out(multiplexer_3_out), .sel(in_19));
  Multiplexer #(.select(2), .width(32), .enable("false")) multiplexer_4 (
    .in0(RT_t), .in1(32'h4), .in2(multiplexer_2_out), .out(multiplexer_4_out), .sel(in_2));  // open: in3
  Multiplexer #(.select(2), .width(32), .enable("false")) multiplexer_5 (
    .in0(PC), .in1(ALU), .in2(Sp), .out(Address), .sel(Address_Selector));  // open: in3
  Multiplexer #(.width(32), .enable("false")) multiplexer_6 (
    .in0({RS_t, TTY_DATA}), .in1(RT_t), .out(Value), .sel(Value_Selector));
  Multiplexer #(.select(2), .width(5), .enable("false")) multiplexer_7 (
    .in0(Rd), .in1(Rt), .in2({5{1'b1}}), .out(multiplexer_7_out), .sel(in_6));  // open: in3
  Multiplexer #(.select(3), .width(32), .enable("false")) multiplexer_8 (
    .in0(ALU), .in1(Data), .in2(Hi), .in3(Lo), .in4(Random_Generator), .in5(KBD), .out(multiplexer_8_out),
    .sel(in_8));  // open: in6, in7
  Register_Bank register_bank_1 (
    .in_1(in_1), .in_2(in_3), .in_3(in_7), .in_4(Rs), .in_5(Rt), .in_6(multiplexer_7_out),
    .in_7(multiplexer_8_out), .out_8({RS_t, TTY_DATA}), .out_9(RT_t), .out_10(Sp));
  ALU alu_1 (
    .in_1(in_1), .in_2(in_12), .in_3(in_11), .ZF(out_27), .SF(out_26), .out_8(out_25), .out_9(alu_1_out_9),
    .out_10(Hi), .out_11(Lo), .in_5(multiplexer_4_out), .in_4(multiplexer_3_out));
  Register #(.width(32)) R_3 (.D(alu_1_out_9), .en(in_10), .Q(ALU), .clk(in_1), .clr(in_3));

  // Other names for the same wires on the sheet: ALU_Result_Enable = in_10; ALU_slc[3:0] = in_11; ALU_Slc_A = in_19;
  //   ALU_Slc_B[1:0] = in_2; Branch_Slc[1:0] = in_4; CLK = in_1; DA_Slc[1:0] = in_6; Data_Slc[2:0] = in_8;
  //   Extend_Slc = in_18; Func[5:0] = Func_Code; HL_En = in_12; Instruction_Enable = in_5;
  //   KBD_ASCII_DATA[6:0] = in_13; KBD_available = in_14; Op[5:0] = Op_Code; PC_Enable = in_17;
  //   RAM_Data[31:0] = in_15; Read_Write = in_7; Reset = in_3; RS_t[6:0] = TTY_DATA

  // Notes on the sheet:
  //   INPUTS
  //   OUTPUTS
endmodule

module UNIT_CONTROL (
  input  in_1,
  input  in_2,
  input  ENTRADAS,
  input  in_4,
  input  in_5,
  input  [5:0] in_6,
  input  [5:0] in_7,
  input  [3:0] in_8,
  input  [3:0] in_9,
  output Output,
  output Output_2,
  output out_12,
  output [1:0] Output_3,
  output Output_4,
  output out_15,
  output [1:0] Output_5,
  output Output_6,
  output out_18,
  output [1:0] Output_7,
  output Output_8,
  output [1:0] Output_9,
  output Output_10,
  output [2:0] Output_11,
  output Output_12,
  output [3:0] Output_13,
  output Output_14,
  output Output_15,
  output Output_16
);

  wire ADR_SRC_0A, ADR_SRC_1A, ADR_SRC_1B, ALU_CALC_0A, ALU_CALC_0B, ALU_CALC_0C, ALU_SRC_B1A, and_1_out,
       ARIT, ARIT_END, ARIT_I, ARIT_I_END, comparator_1_eq, comparator_2_gt, comparator_3_lt, COPIA,
       COPIA_END, CS_1, d_ff_13_q, DA_SLC_0A, DA_SLC_0B, DA_SLC_1A, DA_SLC_1B, DATA_SLC_0A, DATA_SLC_0B,
       DATA_SLC_0D, DECODED_q, demultiplexer_1_out0, demultiplexer_1_out1, demultiplexer_2_out1,
       demultiplexer_3_out1, demultiplexer_4_out0, demultiplexer_4_out1, demultiplexer_5_out0,
       demultiplexer_6_out0, demultiplexer_6_out1, demultiplexer_8_out0, demultiplexer_9_out0,
       demultiplexer_9_out1, demultiplexer_11_out0, demultiplexer_11_out1, demultiplexer_12_out0, ESPECIAL,
       ESPECIAL_END, HALT, IDLE_q, LW, LW_END, or_1_out, or_2_out, or_3_out, or_4_out, or_5_out, or_6_out,
       or_11_out, or_15_out, or_16_out, or_26_out, or_27_out, PCEN_3, PCEN_5, PCEN_7, PILA, R_W_1,
       RESULT_LOAD1, RND, SALTOS, SALTOS_END, START, SW, temp_1_output, temp_2_output, temp_3_output,
       temp_4_output, temp_5_output, TIMER_RESET;
  wire [1:0] ALU_CALC;
  wire [2:0] DEM_SLC;
  wire [3:0] ALU_SLC;

  D_Flip_Flop #(.trigger("falling")) COPY (
    .clk(in_1), .D(COPIA), .Q(Output_11[1]), .reset(in_2));  // open: Qn, preset, en
  Demultiplexer #(.enable("false")) demultiplexer_1 (
    .out0(demultiplexer_1_out0), .out1(demultiplexer_1_out1), .in(PILA), .sel(in_7[0]));
  D_Flip_Flop #(.trigger("falling")) IDLE (
    .clk(in_1), .D(demultiplexer_3_out1), .Q(IDLE_q), .preset(in_2));  // open: Qn, en, reset
  Demultiplexer #(.enable("false")) demultiplexer_2 (
    .out0(DATA_SLC_0A), .out1(demultiplexer_2_out1), .in(Output_11[1]), .sel(comparator_1_eq));
  Comparator #(.width(6)) comparator_1 (.a(in_7), .b(6'b010000), .eq(comparator_1_eq));  // open: gt, lt
  D_Flip_Flop #(.trigger("falling")) d_ff_1 (
    .clk(in_1), .D(LW), .Q(ALU_CALC_0B), .reset(in_2));  // open: Qn, preset, en
  Demultiplexer #(.enable("false")) demultiplexer_3 (
    .out0(TIMER_RESET), .out1(demultiplexer_3_out1), .in(IDLE_q), .sel(in_2));
  D_Flip_Flop #(.trigger("falling")) d_ff_2 (
    .clk(in_1), .D(demultiplexer_1_out1), .Q(ALU_CALC[1]), .reset(in_2));  // open: Qn, preset, en
  or or_1 (or_1_out, demultiplexer_4_out0, demultiplexer_1_out0);
  OP_DECODER op_decoder_1 (
    .in_1(in_6), .in_2(in_7), .in_3(ENTRADAS), .in_4(in_4), .in_5(in_5), .EXTEND_SLC(Output_15),
    .BC_SLC(Output_7), .DEMUL_SLC(DEM_SLC), .ALU_SLC(ALU_SLC));  // open: Output
  or or_2 (or_2_out, DATA_SLC_0A, demultiplexer_2_out1);
  D_Flip_Flop #(.trigger("falling")) d_ff_3 (
    .clk(in_1), .D(or_1_out), .Q(ADR_SRC_1A), .reset(in_2));  // open: Qn, preset, en
  D_Flip_Flop #(.trigger("falling")) END (
    .clk(in_1), .D(or_2_out), .Q(COPIA_END), .reset(in_2));  // open: Qn, preset, en
  or or_3 (or_3_out, demultiplexer_5_out0, START, TIMER_RESET);
  or or_4 (or_4_out, demultiplexer_6_out0, ALU_CALC_0B);
  Demultiplexer #(.enable("false")) demultiplexer_4 (
    .out0(demultiplexer_4_out0), .out1(demultiplexer_4_out1), .in(ADR_SRC_1A), .sel(temp_1_output));
  Temp temp_1 (.in_1(in_8), .in_2(in_1), .in_3(TIMER_RESET), .Output(temp_1_output));
  D_Flip_Flop #(.trigger("falling")) FETCH_INTRUCTION (
    .clk(in_1), .D(or_3_out), .Q(CS_1), .preset(in_2));  // open: Qn, en, reset
  Temp temp_2 (.in_1(in_8), .in_2(in_1), .in_3(TIMER_RESET), .Output(temp_2_output));
  D_Flip_Flop #(.trigger("falling")) READ_RAM (
    .clk(in_1), .D(or_4_out), .Q(ADR_SRC_0A), .reset(in_2));  // open: Qn, preset, en
  Demultiplexer #(.enable("false")) demultiplexer_5 (
    .out0(demultiplexer_5_out0), .out1(Output_14), .in(CS_1), .sel(temp_2_output));
  D_Flip_Flop #(.trigger("falling")) d_ff_4 (
    .clk(in_1), .D(demultiplexer_4_out1), .Q(DATA_SLC_0B), .reset(in_2));  // open: Qn, preset, en
  D_Flip_Flop #(.trigger("falling")) d_ff_5 (
    .clk(in_1), .D(ALU_CALC[1]), .Q(DA_SLC_1B), .reset(in_2));  // open: Qn, preset, en
  D_Flip_Flop #(.trigger("falling")) SALTO (.clk(in_1), .D(SALTOS), .Q(PCEN_3), .reset(in_2));  // open: Qn, preset, en
  Demultiplexer #(.enable("false")) demultiplexer_6 (
    .out0(demultiplexer_6_out0), .out1(demultiplexer_6_out1), .in(ADR_SRC_0A), .sel(temp_3_output));
  Temp temp_3 (.in_1(in_8), .in_2(in_1), .in_3(TIMER_RESET), .Output(temp_3_output));
  D_Flip_Flop #(.trigger("falling")) DECODED (
    .clk(in_1), .D(Output_14), .Q(DECODED_q), .reset(in_2));  // open: Qn, preset, en
  Comparator #(.width(6)) comparator_2 (.a(in_7), .b(6'b010111), .gt(comparator_2_gt));  // open: eq, lt
  Comparator #(.width(6)) comparator_3 (.a(in_7), .b(6'b011100), .lt(comparator_3_lt));  // open: gt, eq
  D_Flip_Flop #(.trigger("falling")) CALCULAR (
    .clk(in_1), .D(ARIT), .Q(RESULT_LOAD1), .reset(in_2));  // open: Qn, preset, en
  and and_1 (and_1_out, comparator_2_gt, comparator_3_lt);
  Demultiplexer #(.select(3), .enable("false")) demultiplexer_7 (
    .out0(ARIT), .out1(COPIA), .out2(SALTOS), .out3(ARIT_I), .out4(PILA), .out5(LW), .out6(SW),
    .out7(ESPECIAL), .in(DECODED_q), .sel(DEM_SLC));
  D_Flip_Flop #(.trigger("falling")) d_ff_6 (.clk(in_1), .D(PCEN_3), .Q(SALTOS_END));  // open: Qn, preset, en, reset
  D_Flip_Flop #(.trigger("falling")) d_ff_7 (
    .clk(in_1), .D(DATA_SLC_0B), .Q(ALU_CALC_0A), .reset(in_2));  // open: Qn, preset, en
  or or_5 (or_5_out, demultiplexer_9_out0, DA_SLC_1B);
  Demultiplexer #(.enable("false")) demultiplexer_8 (
    .out0(demultiplexer_8_out0), .out1(out_18), .in(RESULT_LOAD1), .sel(and_1_out));
  D_Flip_Flop #(.trigger("falling")) WRITE_REG (
    .clk(in_1), .D(demultiplexer_6_out1), .Q(DA_SLC_0B), .reset(in_2));  // open: Qn, preset, en
  D_Flip_Flop #(.trigger("falling")) d_ff_8 (
    .clk(in_1), .D(or_5_out), .Q(ADR_SRC_1B), .reset(in_2));  // open: Qn, preset, en
  D_Flip_Flop #(.trigger("falling")) WRITE_REG_2 (
    .clk(in_1), .D(demultiplexer_8_out0), .Q(R_W_1), .reset(in_2));  // open: Qn, preset, en
  D_Flip_Flop #(.trigger("falling")) CALCULATE (
    .clk(in_1), .D(ARIT_I), .Q(ALU_SRC_B1A), .reset(in_2));  // open: Qn, preset, en
  Demultiplexer #(.enable("false")) demultiplexer_9 (
    .out0(demultiplexer_9_out0), .out1(demultiplexer_9_out1), .in(ADR_SRC_1B), .sel(temp_4_output));
  Temp temp_4 (.in_1(in_9), .in_2(in_1), .in_3(TIMER_RESET), .Output(temp_4_output));
  D_Flip_Flop #(.trigger("falling")) d_ff_9 (
    .clk(in_1), .D(DA_SLC_0B), .Q(LW_END), .reset(in_2));  // open: Qn, preset, en
  or or_6 (or_6_out, R_W_1, out_18);
  or or_7 (START, ARIT_END, COPIA_END, SALTOS_END, ARIT_I_END, PCEN_5, LW_END, PCEN_7, ESPECIAL_END);
  D_Flip_Flop #(.trigger("falling")) WRITE_REG_3 (
    .clk(in_1), .D(ALU_SRC_B1A), .Q(DA_SLC_0A), .reset(in_2));  // open: Qn, preset, en
  D_Flip_Flop #(.trigger("falling")) END_2 (
    .clk(in_1), .D(or_6_out), .Q(ARIT_END), .reset(in_2));  // open: Qn, preset, en
  D_Flip_Flop #(.trigger("falling")) d_ff_10 (
    .clk(in_1), .D(ALU_CALC_0A), .Q(DA_SLC_1A), .reset(in_2));  // open: Qn, preset, en
  D_Flip_Flop #(.trigger("falling")) d_ff_11 (
    .clk(in_1), .D(SW), .Q(ALU_CALC_0C), .reset(in_2));  // open: Qn, preset, en
  or or_8 (out_15, CS_1, ADR_SRC_1A, ADR_SRC_1B, ADR_SRC_0A, Output_10);
  or or_9 (Output_2, R_W_1, Output_11[1], DA_SLC_0A, DATA_SLC_0B, DA_SLC_1B, DA_SLC_1A, DA_SLC_0B, Output_11[2]);
  or or_10 (out_12, ADR_SRC_1B, Output_10);
  D_Flip_Flop #(.trigger("falling")) END_3 (
    .clk(in_1), .D(DA_SLC_0A), .Q(ARIT_I_END), .reset(in_2));  // open: Qn, preset, en
  or or_11 (or_11_out, DA_SLC_1A, demultiplexer_9_out1);
  D_Flip_Flop #(.trigger("falling")) d_ff_12 (
    .clk(in_1), .D(or_11_out), .Q(PCEN_5), .reset(in_2));  // open: Qn, preset, en
  or or_12 (Output_11[0], DATA_SLC_0A, DATA_SLC_0B, DA_SLC_0B, DATA_SLC_0D);
  or or_13 (Output_4, ARIT_END, COPIA_END, PCEN_3, ARIT_I_END, PCEN_5, LW_END, PCEN_7, ESPECIAL_END);
  or or_14 (Output_16, RESULT_LOAD1, ALU_SRC_B1A, ALU_CALC_0A, ALU_CALC[1], ALU_CALC_0B, ALU_CALC_0C);
  D_Flip_Flop #(.trigger("falling")) d_ff_13 (
    .clk(in_1), .D(ESPECIAL), .Q(d_ff_13_q), .reset(in_2));  // open: Qn, preset, en
  or or_15 (or_15_out, Output_8, HALT);
  or or_16 (or_16_out, demultiplexer_11_out0, ALU_CALC_0C);
  Multiplexer #(.select(2), .width(4), .enable("false")) multiplexer_1 (
    .in0(ALU_SLC), .in1(4'b0110), .in2(4'b0111), .out(Output_13), .sel(ALU_CALC));  // open: in3
  Demultiplexer #(.select(2), .enable("false")) demultiplexer_10 (
    .out0(Output_6), .out1(RND), .out2(Output_12), .out3(HALT), .in(d_ff_13_q), .sel(in_7[2:1]));
  D_Flip_Flop #(.trigger("falling")) d_ff_14 (
    .clk(in_1), .D(or_15_out), .Q(Output_8), .reset(in_2));  // open: Qn, preset, en
  D_Flip_Flop #(.trigger("falling")) d_ff_15 (
    .clk(in_1), .D(or_16_out), .Q(Output_10), .reset(in_2));  // open: Qn, preset, en
  or or_17 (Output_3[0], ALU_CALC_0A, ALU_CALC[1]);
  or or_18 (Output_3[1], ALU_SRC_B1A, ALU_CALC_0B, ALU_CALC_0C);
  Temp temp_5 (.in_1(in_9), .in_2(in_1), .in_3(TIMER_RESET), .Output(temp_5_output));
  or or_19 (Output_9[0], DA_SLC_0A, DA_SLC_0B);
  or or_20 (Output_9[1], DA_SLC_1A, DA_SLC_1B);
  or or_21 (Output_11[2], RND, Output_12);
  Demultiplexer #(.enable("false")) demultiplexer_11 (
    .out0(demultiplexer_11_out0), .out1(demultiplexer_11_out1), .in(Output_10), .sel(temp_5_output));
  or or_22 (Output, ALU_CALC_0A, ALU_CALC[1]);
  or or_23 (ALU_CALC[0], ALU_CALC_0A, ALU_CALC_0B, ALU_CALC_0C);
  or or_24 (Output_5[1], ADR_SRC_1A, ADR_SRC_1B);
  or or_25 (Output_5[0], ADR_SRC_0A, Output_10);
  D_Flip_Flop #(.trigger("falling")) d_ff_16 (
    .clk(in_1), .D(demultiplexer_11_out1), .Q(PCEN_7));  // open: Qn, preset, en, reset
  Demultiplexer #(.enable("false")) demultiplexer_12 (
    .out0(demultiplexer_12_out0), .out1(DATA_SLC_0D), .in(Output_11[2]), .sel(Output_12));
  or or_26 (or_26_out, demultiplexer_12_out0, DATA_SLC_0D);
  or or_27 (or_27_out, or_26_out, Output_6);
  D_Flip_Flop #(.trigger("falling")) d_ff_17 (
    .clk(in_1), .D(or_27_out), .Q(ESPECIAL_END), .reset(in_2));  // open: Qn, preset, en

  // Other names for the same wires on the sheet: ADR_SRC[1:0] = Output_5; ADR_SRC_0 = Output_5[0];
  //   ADR_SRC_1 = Output_5[1]; ALU_CALC_0 = ALU_CALC[0]; ALU_CALC_1 = ALU_CALC[1]; ALU_SRC_A2 = ALU_CALC[1];
  //   ALU_SRC_B0B = ALU_CALC[1]; RESULT_LOAD4 = ALU_CALC[1]; ALU_CONTROL[3:0] = Output_13; ALU_SRC_A = Output;
  //   ALU_SRC_B[1:0] = Output_3; ALU_SRC_B0 = Output_3[0]; ALU_SRC_B1 = Output_3[1]; BC_SLC[1:0] = Output_7;
  //   CLK = in_1; CS = out_15; CS_2 = ADR_SRC_1A; CS_4 = ADR_SRC_0A; DA_SLC[1:0] = Output_9; DA_SLC_0 = Output_9[0];
  //   DA_SLC_1 = Output_9[1]; DATA_SLC[2:0] = Output_11; DATA_SLC_0 = Output_11[0]; DATA_SLC_1 = Output_11[1];
  //   R_W_2 = Output_11[1]; DATA_SLC_2 = Output_11[2]; R_W_8 = Output_11[2]; EQF = in_5; EXTEND_SLC = Output_15;
  //   FUNC_CODE[5:0] = in_7; HI_LOW_LOAD = out_18; IN_EN = Output_14; KBD = Output_12; NF = in_4; OP_CODE[5:0] = in_6;
  //   PC_EN = Output_4; PCEN_1 = ARIT_END; PCEN_2 = COPIA_END; PCEN_4 = ARIT_I_END; PCEN_6 = LW_END;
  //   PCEN_8 = ESPECIAL_END; PILA_END = PCEN_5; R_W = Output_2; R_W_3 = DA_SLC_0A; R_W_4 = DATA_SLC_0B;
  //   R_W_5 = DA_SLC_1B; R_W_6 = DA_SLC_1A; DATA_SLC_0C = DA_SLC_0B; R_W_7 = DA_SLC_0B; READ_TIME[3:0] = in_8;
  //   RESET = in_2; RESULT_LOAD = Output_16; RESULT_LOAD2 = ALU_SRC_B1A; ALU_SRC_A1 = ALU_CALC_0A;
  //   ALU_SRC_B0A = ALU_CALC_0A; RESULT_LOAD3 = ALU_CALC_0A; ALU_SRC_B1B = ALU_CALC_0B; RESULT_LOAD5 = ALU_CALC_0B;
  //   ALU_SRC_B1C = ALU_CALC_0C; RESULT_LOAD6 = ALU_CALC_0C; STOP = Output_8; SW_END = PCEN_7; TTY = Output_6;
  //   TTY_ENABLE = Output_6; WRITE = out_12; CS_3 = ADR_SRC_1B; WRITE_1 = ADR_SRC_1B; ADR_SRC_0B = Output_10;
  //   CS_5 = Output_10; VALUE_SRC = Output_10; WRITE_2 = Output_10; WRITE_TIME[3:0] = in_9; ZF = ENTRADAS

  // Notes on the sheet:
  //   COPIAR
  //   SALIDAS
  //   CONTROL UNIT
  //   LW
  //   SALTOS
  //   PILA
  //   ARITMETICA
  //   ARITMETICA I
  //   ENABLER
  //   SELECTOR
  //   SW
  //   ESPECIAL
endmodule

module OP_DECODER (
  input  [5:0] in_1,
  input  [5:0] in_2,
  input  in_3,
  input  in_4,
  input  in_5,
  output EXTEND_SLC,
  output [1:0] BC_SLC,
  output [2:0] DEMUL_SLC,
  output [3:0] ALU_SLC,
  output [2:0] Output
);

  wire _00_0000, _11_1000, _11_1111, ADD, ADDI, AND, and_7_out, and_8_out, and_9_out, and_10_out, and_11_out,
       and_28_out, and_29_out, ANDI, ARIT_I, ARITMETICA, BEQ, BGTZ, BLEZ, BLTZ, BNE, comparator_4_eq,
       comparator_5_eq, comparator_6_eq, comparator_7_eq, comparator_8_eq, comparator_9_eq, comparator_10_eq,
       comparator_11_eq, comparator_12_eq, comparator_13_eq, comparator_14_eq, comparator_15_eq,
       comparator_16_eq, comparator_17_eq, comparator_18_eq, comparator_19_eq, comparator_20_eq,
       comparator_21_eq, comparator_22_eq, comparator_23_eq, comparator_24_eq, comparator_25_eq,
       comparator_26_lt, comparator_27_eq, comparator_27_gt, comparator_28_lt, comparator_29_gt,
       comparator_30_lt, comparator_31_gt, COPIA, DIV, HALT, IDIV, IMUL, ISLT, ISLTI, J, JR, KBD, LW, MFHI,
       MFLO, MUL, NOP, NOR, OR, or_2_out, ORI, POP, PUSH, RND, RS____0_t, RS_____0, RS______RT, SALTOS, SLT,
       SLTI, SUB, SW, TTY, XOR, XORI;

  Comparator #(.width(6)) comparator_1 (.a(in_1), .b({6{1'b0}}), .eq(_00_0000));  // open: gt, lt
  Comparator #(.width(6)) comparator_2 (.a(in_1), .b({6{1'b1}}), .eq(_11_1111));  // open: gt, lt
  Comparator #(.width(6)) comparator_3 (.a(in_1), .b(6'b111000), .eq(_11_1000));  // open: gt, lt
  not not_1 (RS______RT, in_5);
  Comparator #(.width(6)) comparator_4 (.a(in_2), .b(6'b100000), .eq(comparator_4_eq));  // open: gt, lt
  Comparator #(.width(6)) comparator_5 (.a(in_2), .b(6'b100010), .eq(comparator_5_eq));  // open: gt, lt
  Comparator #(.width(6)) comparator_6 (.a(in_2), .b(6'b011000), .eq(comparator_6_eq));  // open: gt, lt
  Comparator #(.width(6)) comparator_7 (.a(in_2), .b(6'b011001), .eq(comparator_7_eq));  // open: gt, lt
  Comparator #(.width(6)) comparator_8 (.a(in_2), .b(6'b011010), .eq(comparator_8_eq));  // open: gt, lt
  Comparator #(.width(6)) comparator_9 (.a(in_2), .b(6'b011011), .eq(comparator_9_eq));  // open: gt, lt
  or or_1 (RS_____0, in_3, in_4);
  not not_2 (RS____0_t, RS_____0);
  and and_1 (ADD, _00_0000, comparator_4_eq);
  and and_2 (SUB, _00_0000, comparator_5_eq);
  and and_3 (IMUL, _00_0000, comparator_6_eq);
  and and_4 (MUL, _00_0000, comparator_7_eq);
  and and_5 (IDIV, _00_0000, comparator_8_eq);
  and and_6 (DIV, _00_0000, comparator_9_eq);
  Comparator #(.width(6)) comparator_10 (.a(in_2), .b(6'b100100), .eq(comparator_10_eq));  // open: gt, lt
  Comparator #(.width(6)) comparator_11 (.a(in_2), .b(6'b100101), .eq(comparator_11_eq));  // open: gt, lt
  Comparator #(.width(6)) comparator_12 (.a(in_2), .b(6'b100111), .eq(comparator_12_eq));  // open: gt, lt
  Comparator #(.width(6)) comparator_13 (.a(in_2), .b(6'b101000), .eq(comparator_13_eq));  // open: gt, lt
  and and_7 (and_7_out, BEQ, in_5);
  and and_8 (and_8_out, BNE, RS______RT);
  and and_9 (and_9_out, BLEZ, RS_____0);
  and and_10 (and_10_out, BGTZ, RS____0_t);
  and and_11 (and_11_out, BLTZ, in_4);
  and and_12 (AND, _00_0000, comparator_10_eq);
  and and_13 (OR, _00_0000, comparator_11_eq);
  and and_14 (NOR, _00_0000, comparator_12_eq);
  and and_15 (XOR, _00_0000, comparator_13_eq);
  or or_2 (or_2_out, and_7_out, and_8_out, and_9_out, and_10_out, and_11_out);
  Comparator #(.width(6)) comparator_14 (.a(in_2), .b(6'b101010), .eq(comparator_14_eq));  // open: gt, lt
  Comparator #(.width(6)) comparator_15 (.a(in_2), .b(6'b101011), .eq(comparator_15_eq));  // open: gt, lt
  Comparator #(.width(6)) comparator_16 (.a(in_2), .b(6'b010000), .eq(comparator_16_eq));  // open: gt, lt
  Comparator #(.width(6)) comparator_17 (.a(in_2), .b(6'b010010), .eq(comparator_17_eq));  // open: gt, lt
  Comparator #(.width(6)) comparator_18 (.a(in_2), .b({6{1'b0}}), .eq(comparator_18_eq));  // open: gt, lt
  Comparator #(.width(6)) comparator_19 (.a(in_2), .b(6'b001000), .eq(comparator_19_eq));  // open: gt, lt
  or or_3 (BC_SLC[0], or_2_out, JR);
  or or_4 (BC_SLC[1], JR, J);
  and and_16 (ISLT, _00_0000, comparator_14_eq);
  and and_17 (SLT, _00_0000, comparator_15_eq);
  and and_18 (MFHI, _00_0000, comparator_16_eq);
  and and_19 (MFLO, _00_0000, comparator_17_eq);
  and and_20 (NOP, _00_0000, comparator_18_eq);
  and and_21 (JR, _00_0000, comparator_19_eq);
  Comparator #(.width(6)) comparator_20 (.a(in_2), .b({6{1'b1}}), .eq(comparator_20_eq));  // open: gt, lt
  Comparator #(.width(6)) comparator_21 (.a(in_2), .b(6'b000001), .eq(comparator_21_eq));  // open: gt, lt
  Comparator #(.width(6)) comparator_22 (.a(in_2), .b(6'b000010), .eq(comparator_22_eq));  // open: gt, lt
  Comparator #(.width(6)) comparator_23 (.a(in_2), .b(6'b000100), .eq(comparator_23_eq));  // open: gt, lt
  Comparator #(.width(6)) comparator_24 (.a(in_2), .b({6{1'b0}}), .eq(comparator_24_eq));  // open: gt, lt
  Comparator #(.width(6)) comparator_25 (.a(in_2), .b(6'b000001), .eq(comparator_25_eq));  // open: gt, lt
  and and_22 (HALT, _11_1111, comparator_20_eq);
  and and_23 (TTY, _11_1111, comparator_21_eq);
  and and_24 (RND, _11_1111, comparator_22_eq);
  and and_25 (KBD, _11_1111, comparator_23_eq);
  and and_26 (POP, _11_1000, comparator_24_eq);
  and and_27 (PUSH, _11_1000, comparator_25_eq);
  Comparator #(.width(6), .mode("unsigned")) comparator_26 (
    .a(in_1), .b(6'b001000), .lt(comparator_26_lt));  // open: gt, eq
  Comparator #(.width(6), .mode("unsigned")) comparator_27 (
    .a(in_1), .b({6{1'b0}}), .gt(comparator_27_gt), .eq(comparator_27_eq));  // open: lt
  Comparator #(.width(6), .mode("unsigned")) comparator_28 (
    .a(in_2), .b(6'b001001), .lt(comparator_28_lt));  // open: gt, eq
  Comparator #(.width(6), .mode("unsigned")) comparator_29 (
    .a(in_2), .b(6'b001111), .gt(comparator_29_gt));  // open: eq, lt
  Comparator #(.width(6), .mode("unsigned")) comparator_30 (
    .a(in_2), .b(6'b010011), .lt(comparator_30_lt));  // open: gt, eq
  Comparator #(.width(6), .mode("unsigned")) comparator_31 (
    .a(in_2), .b(6'b010111), .gt(comparator_31_gt));  // open: eq, lt
  and and_28 (and_28_out, comparator_26_lt, comparator_27_gt);
  and and_29 (and_29_out, comparator_27_eq, comparator_28_lt);
  and and_30 (COPIA, comparator_27_eq, comparator_29_gt, comparator_30_lt);
  and and_31 (ARITMETICA, comparator_27_eq, comparator_31_gt);
  or or_5 (SALTOS, and_28_out, and_29_out);
  Comparator #(.width(6)) comparator_32 (.a(in_1), .b(6'b001000), .eq(ADDI));  // open: gt, lt
  Comparator #(.width(6)) comparator_33 (.a(in_1), .b(6'b001100), .eq(ANDI));  // open: gt, lt
  Comparator #(.width(6)) comparator_34 (.a(in_1), .b(6'b001101), .eq(ORI));  // open: gt, lt
  Comparator #(.width(6)) comparator_35 (.a(in_1), .b(6'b001110), .eq(XORI));  // open: gt, lt
  Comparator #(.width(6)) comparator_36 (.a(in_1), .b(6'b001010), .eq(ISLTI));  // open: gt, lt
  Comparator #(.width(6)) comparator_37 (.a(in_1), .b(6'b001011), .eq(SLTI));  // open: gt, lt
  Comparator #(.width(6)) comparator_38 (.a(in_1), .b(6'b000100), .eq(BEQ));  // open: gt, lt
  Comparator #(.width(6)) comparator_39 (.a(in_1), .b(6'b000101), .eq(BNE));  // open: gt, lt
  Comparator #(.width(6)) comparator_40 (.a(in_1), .b(6'b000110), .eq(BLEZ));  // open: gt, lt
  Comparator #(.width(6)) comparator_41 (.a(in_1), .b(6'b000111), .eq(BGTZ));  // open: gt, lt
  Comparator #(.width(6)) comparator_42 (.a(in_1), .b(6'b000001), .eq(BLTZ));  // open: gt, lt
  Comparator #(.width(6)) comparator_43 (.a(in_1), .b(6'b100011), .eq(LW));  // open: gt, lt
  Comparator #(.width(6)) comparator_44 (.a(in_1), .b(6'b101011), .eq(SW));  // open: gt, lt
  or or_6 (DEMUL_SLC[0], COPIA, ARIT_I, LW, _11_1111);
  or or_7 (DEMUL_SLC[1], SALTOS, ARIT_I, SW, _11_1111);
  or or_8 (DEMUL_SLC[2], _11_1000, LW, SW, _11_1111);
  Comparator #(.width(6)) comparator_45 (.a(in_1), .b(6'b000010), .eq(J));  // open: gt, lt
  or or_9 (EXTEND_SLC, ANDI, ORI, XORI);
  ALU_ENCODER alu_encoder_1 (
    .ADD(ADD), .ADDI(ADDI), .SUB(SUB), .IMUL(IMUL), .MUL(MUL), .IDIV(IDIV), .DIV(DIV), .AND(AND),
    .ANDI(ANDI), .OR(OR), .ORI(ORI), .XOR(XOR), .NOR(NOR), .XORI(XORI), .ISLT(ISLT), .ISLTI(ISLTI),
    .SLT(SLT), .SLTI(SLTI), .Tipe_I(ARIT_I), .ALU_SELECTOR(ALU_SLC));

  assign Output = DEMUL_SLC;

  // Other names for the same wires on the sheet: EXT_SLC = EXTEND_SLC; FUNC_CODE[5:0] = in_2; OP_CODE[5:0] = in_1;
  //   NF = in_4; RS____0 = in_4; EQF = in_5; RS_____RT = in_5; ZF = in_3

  // Notes on the sheet:
  //   ENTRADAS
  //   ARITMETICAS
  //   SALIDAS
  //   LOGICA
  //   BRANCH CONTROL SELECTOR
  //   COPIAR REGISTROS
  //   SALTOS
  //   COMPARACIONES
  //   TIPO R
  //   ESPECIAL
  //   MEMORIA
  //   ARITMETICAS
  //   LOGICA
  //   COMPARACIONES
  //   TIPO I
  //   SALTOS
  //   MEMORIA
  //   TIPO J
endmodule

module ALU_ENCODER (
  input  ADD,
  input  ADDI,
  input  SUB,
  input  IMUL,
  input  MUL,
  input  IDIV,
  input  DIV,
  input  AND,
  input  ANDI,
  input  OR,
  input  ORI,
  input  XOR,
  input  NOR,
  input  XORI,
  input  ISLT,
  input  ISLTI,
  input  SLT,
  input  SLTI,
  output Tipe_I,
  output [3:0] ALU_SELECTOR
);

  wire ADD_t, AND_t, ISLT_t, OR_t, SLT_t, XOR_t;

  or or_1 (ADD_t, ADD, ADDI);
  or or_2 (AND_t, AND, ANDI);
  or or_3 (OR_t, OR, ORI);
  or or_4 (XOR_t, XOR, XORI);
  or or_5 (ISLT_t, ISLT, ISLTI);
  or or_6 (SLT_t, SLT, SLTI);
  or or_7 (Tipe_I, ADDI, ANDI, ORI, XORI, SLTI, ISLTI);
  or or_8 (ALU_SELECTOR[3], IMUL, MUL, IDIV, DIV);
  or or_9 (ALU_SELECTOR[2], ISLT_t, SLT_t, ADD_t, SUB);
  or or_10 (ALU_SELECTOR[1], NOR, XOR_t, ADD_t, SUB, IDIV, DIV);
  or or_11 (ALU_SELECTOR[0], OR_t, XOR_t, SLT_t, SUB, MUL, DIV);

  // Notes on the sheet:
  //   ALU Enconder
endmodule

module LITTLE_ENDIAN_BIG (
  input  [31:0] ENTRADA,
  output [31:0] SALIDA
);


  assign SALIDA = {ENTRADA[7:0], ENTRADA[15:8], ENTRADA[23:16], ENTRADA[31:24]};
endmodule

module WRITE_RAM (
  input  [31:0] VALOR,
  input  [31:0] MEMORIA,
  output [31:0] INPUT1,
  output [3:0] MASK,
  output [31:0] INPUT2,
  output [15:0] ADDRESS,
  output [31:0] INPUT3,
  output [31:0] INPUT4
);

  wire [31:0] little_endian_big_1_salida;

  LITTLE_ENDIAN_BIG little_endian_big_1 (.ENTRADA(VALOR), .SALIDA(little_endian_big_1_salida));
  Demultiplexer #(.select(2), .width(32), .enable("false")) demultiplexer_1 (
    .out0(INPUT1), .out1(INPUT2), .out2(INPUT3), .out3(INPUT4), .in(little_endian_big_1_salida),
    .sel(MEMORIA[3:2]));
  Demultiplexer #(.select(2), .enable("false")) demultiplexer_2 (
    .out0(MASK[0]), .out1(MASK[1]), .out2(MASK[2]), .out3(MASK[3]), .in(1'b1), .sel(MEMORIA[3:2]));

  assign ADDRESS = MEMORIA[19:4];

  // Other names for the same wires on the sheet: SLECTOR[1:0] = MEMORIA[3:2]

  // Notes on the sheet:
  //   ENTRADAS
  //   WRITE
  //   SALIDAS
endmodule

module READ_RAM (
  input  [31:0] in_1,
  input  [31:0] in_2,
  input  [31:0] in_3,
  input  [31:0] in_4,
  input  [31:0] in_5,
  output [31:0] RAM_DATA
);

  wire [31:0] multiplexer_1_out;

  Multiplexer #(.select(2), .width(32), .enable("false")) multiplexer_1 (
    .in0(in_1), .in1(in_3), .in2(in_4), .in3(in_5), .out(multiplexer_1_out), .sel(in_2[3:2]));
  LITTLE_ENDIAN_BIG little_endian_big_1 (.ENTRADA(multiplexer_1_out), .SALIDA(RAM_DATA));

  // Other names for the same wires on the sheet: BANK0[31:0] = in_1; BANK1[31:0] = in_3; BANK2[31:0] = in_4;
  //   BANK3[31:0] = in_5; SELECTOR[1:0] = in_2[3:2]
endmodule

module Temp (
  input  [3:0] in_1,
  input  in_2,
  input  in_3,
  output Output
);

  wire [3:0] counter_1_q;

  Counter #(.width(4), .max('hf)) counter_1 (
    .count(1'b1), .Q(counter_1_q), .clk(in_2), .clr(in_3));  // open: load, D, carry
  Comparator #(.width(4)) comparator_1 (.a(in_1), .b(counter_1_q), .eq(Output));  // open: gt, lt
endmodule

module ALU (
  input  in_1,
  input  in_2,
  input  [3:0] in_3,
  input  [31:0] in_4,
  input  [31:0] in_5,
  output ZF,
  output SF,
  output out_8,
  output [31:0] out_9,
  output [31:0] out_10,
  output [31:0] out_11
);

  wire comparator_1_lt, comparator_2_lt;
  wire [1:0] SELECTOR_MULT_DIV;
  wire [31:0] ADD, AND, multiplexer_2_out, multiplexer_3_out, MUX_1_1, MUX_1_2, MUX_1_3, MUX_1_4, MUX_2_1,
       MUX_2_2, MUX_2_3, MUX_2_4, NOR, OR, SLT, SLTU, SUB, XOR;

  assign AND = in_4 & in_5;  // AND_Gate and_1, 32 bits wide
  assign OR = in_4 | in_5;  // OR_Gate or_1, 32 bits wide
  assign NOR = ~(in_4 | in_5);  // NOR_Gate nor_1, 32 bits wide
  assign XOR = in_4 ^ in_5;  // XOR_Gate xor_1, 32 bits wide
  Comparator #(.width(32)) comparator_1 (.a(in_4), .b(in_5), .eq(out_8), .lt(comparator_1_lt));  // open: gt
  Comparator #(.width(32), .mode("unsigned")) comparator_2 (.a(in_4), .b(in_5), .lt(comparator_2_lt));  // open: gt, eq
  Adder #(.width(32)) adder_1 (.a(in_4), .b(in_5), .out(ADD));  // open: cin, cout
  Subtractor #(.width(32)) subtractor_1 (.a(in_4), .b(in_5), .out(SUB));  // open: bin, bout
  Signed_Multipler signed_multipler_1 (.in_1(in_4), .in_2(in_5), .out_3(MUX_2_1), .out_4(MUX_1_1));
  Multiplier #(.width(32)) multiplier_1 (.a(in_4), .b(in_5), .out(MUX_2_2), .cout(MUX_1_2));  // open: cin
  Signed_Divider signed_divider_1 (.in_1(in_4), .in_2(in_5), .out_3(MUX_2_3), .out_4(MUX_1_3));
  Divider #(.width(32)) divider_1 (.a(in_4), .b(in_5), .out(MUX_2_4), .rem(MUX_1_4));  // open: upper
  assign SLT = {{31{1'b0}}, comparator_1_lt};  // Bit_Extender bit_extender_1
  assign SLTU = {{31{1'b0}}, comparator_2_lt};  // Bit_Extender bit_extender_2
  and and_2 (SELECTOR_MULT_DIV[0], in_3[3], ~in_3[2], in_3[0]);  // AND_Gate
  and and_3 (SELECTOR_MULT_DIV[1], in_3[1], ~in_3[2], in_3[3]);  // AND_Gate
  Comparator #(.width(32)) comparator_3 (.a(in_4), .b({32{1'b0}}), .eq(ZF), .lt(SF));  // open: gt
  Multiplexer #(.select(4), .width(32), .enable("false")) multiplexer_1 (
    .in0(AND), .in1(OR), .in2(NOR), .in3(XOR), .in4(SLT), .in5(SLTU), .in6(ADD), .in7(SUB), .out(out_9),
    .sel(in_3));  // open: in8, in9, in10, in11, in12, in13, in14, in15
  Multiplexer #(.select(2), .width(32), .enable("false")) multiplexer_2 (
    .in0(MUX_1_1), .in1(MUX_1_2), .in2(MUX_1_3), .in3(MUX_1_4), .out(multiplexer_2_out),
    .sel(SELECTOR_MULT_DIV));
  Multiplexer #(.select(2), .width(32), .enable("false")) multiplexer_3 (
    .in0(MUX_2_1), .in1(MUX_2_2), .in2(MUX_2_3), .in3(MUX_2_4), .out(multiplexer_3_out),
    .sel(SELECTOR_MULT_DIV));
  Register #(.width(32)) register_1 (.D(multiplexer_2_out), .en(in_2), .Q(out_10), .clk(in_1));  // open: clr
  Register #(.width(32)) register_2 (.D(multiplexer_3_out), .en(in_2), .Q(out_11), .clk(in_1));  // open: clr

  // Other names for the same wires on the sheet: A[31:0] = in_4; ALU_SELECTOR[3:0] = in_3; B[31:0] = in_5; CLK = in_1;
  //   ENABLE_HIGH_LOW = in_2; EQF = out_8; HIGH[31:0] = out_10; LOW[31:0] = out_11; Output[31:0] = out_9

  // Notes on the sheet:
  //   INPUTS
  //   OUTPUTS
  //   ALU
endmodule

module Branch_Control (
  input  [31:0] in_1,
  input  [15:0] in_2,
  input  [25:0] in_3,
  input  [31:0] in_4,
  input  [1:0] in_5,
  output [31:0] out_6
);

  wire [15:0] multiplier_1_out;
  wire [31:0] bit_extender_1_out, PC_4, PC___4___Offset___4;

  Multiplier #(.width(16)) multiplier_1 (.a(in_2), .b(16'h4), .out(multiplier_1_out));  // open: cin, cout
  Adder #(.width(32)) adder_1 (.a(in_1), .b(32'h4), .out(PC_4));  // open: cin, cout
  assign bit_extender_1_out = {{16{multiplier_1_out[15]}}, multiplier_1_out};  // Bit_Extender bit_extender_1
  Adder #(.width(32)) adder_2 (.a(PC_4), .b(bit_extender_1_out), .out(PC___4___Offset___4));  // open: cin, cout
  Multiplexer #(.select(2), .width(32), .enable("false")) multiplexer_1 (
    .in0(PC_4), .in1(PC___4___Offset___4), .in2({in_1[31:28], in_3, 2'b00}), .in3(in_4), .out(out_6),
    .sel(in_5));

  // Other names for the same wires on the sheet: BS[1:0] = in_5; Destination[25:0] = in_3;
  //   Jump[31:2] = {in_1[31:28], in_3}; PC[31:0] = in_1; Offset[15:0] = in_2; PC_star[31:0] = out_6; Rs[31:0] = in_4

  // Notes on the sheet:
  //   Inputs
  //   Output
  //   Branch Control
endmodule

module PC (
  input  [31:0] PC_in,
  input  Enable,
  input  CLK,
  input  Reset,
  output [31:0] PC_out
);

  Register #(.width(32)) PC (.D(PC_in), .en(Enable), .Q(PC_out), .clk(CLK), .clr(Reset));

  // Notes on the sheet:
  //   Program Counter
endmodule

module Instruction_Decoder (
  input  [31:0] in_1,
  output [5:0] out_2,
  output [25:0] out_3,
  output [4:0] out_4,
  output [4:0] out_5,
  output [15:0] out_6,
  output [4:0] out_7,
  output [5:0] out_8
);


  assign out_2 = in_1[31:26];
  assign out_3 = in_1[25:0];
  assign out_4 = in_1[25:21];
  assign out_5 = in_1[20:16];
  assign out_6 = in_1[15:0];
  assign out_7 = in_1[15:11];
  assign out_8 = in_1[5:0];

  // Other names for the same wires on the sheet: Const[15:0] = in_1[15:0]; Destination_Jump[25:0] = in_1[25:0];
  //   Func_Code[5:0] = in_1[5:0]; Rd[4:0] = in_1[15:11]; Rt[4:0] = in_1[20:16]; Rs[4:0] = in_1[25:21];
  //   Op_Code[5:0] = in_1[31:26]

  // Notes on the sheet:
  //   Instruction Decoder
  //   OutPuts
endmodule

module Signed_Multipler (
  input  [31:0] in_1,
  input  [31:0] in_2,
  output [31:0] out_3,
  output [31:0] out_4
);

  wire adder_1_cout, SIGN;
  wire [31:0] adder_1_out, adder_2_out, In_Mult1, In_Mult2, multiplier_1_cout, multiplier_1_out,
       negator_1_out, negator_2_out, not_1_out, not_2_out;

  // Probe on in_1
  // Probe on in_2
  Multiplier #(.width(32)) multiplier_1 (
    .a(In_Mult1), .b(In_Mult2), .out(multiplier_1_out), .cout(multiplier_1_cout));  // open: cin
  Negator #(.width(32)) negator_1 (.in(in_1), .out(negator_1_out));
  Negator #(.width(32)) negator_2 (.in(in_2), .out(negator_2_out));
  assign not_1_out = ~multiplier_1_out;  // NOT_Gate not_1, 32 bits wide
  assign not_2_out = ~multiplier_1_cout;  // NOT_Gate not_2, 32 bits wide
  Multiplexer #(.width(32), .enable("false")) multiplexer_1 (
    .in0(in_1), .in1(negator_1_out), .out(In_Mult1), .sel(in_1[31]));
  Multiplexer #(.width(32), .enable("false")) multiplexer_2 (
    .in0(in_2), .in1(negator_2_out), .out(In_Mult2), .sel(in_2[31]));
  Adder #(.width(32)) adder_1 (.a(not_1_out), .b(32'h1), .out(adder_1_out), .cout(adder_1_cout));  // open: cin
  Adder #(.width(32)) adder_2 (.a(not_2_out), .b({32{1'b0}}), .out(adder_2_out), .cin(adder_1_cout));  // open: cout
  // Probe on out_3
  Multiplexer #(.width(32), .enable("false")) multiplexer_3 (
    .in0(multiplier_1_out), .in1(adder_1_out), .out(out_3), .sel(SIGN));
  Multiplexer #(.width(32), .enable("false")) multiplexer_4 (
    .in0(multiplier_1_cout), .in1(adder_2_out), .out(out_4), .sel(SIGN));
  // Probe on out_4
  xor xor_1 (SIGN, in_1[31], in_2[31]);

  // Other names for the same wires on the sheet: Carry_Out[31:0] = out_4; Input1[31:0] = in_1; Sign1 = in_1[31];
  //   Input2[31:0] = in_2; Sign2 = in_2[31]; Result[31:0] = out_3

  // Notes on the sheet:
  //   INPUT
  //   OUTPUT
  //   Part1
  //   Part2
  //   Separador
  //   Separador
  //   SIGN
endmodule

module Signed_Divider (
  input  [31:0] in_1,
  input  [31:0] in_2,
  output [31:0] out_3,
  output [31:0] out_4
);

  wire xor_1_out;
  wire [31:0] divider_1_out, In_Div1, In_Div2, negator_1_out, negator_2_out, negator_3_out;

  // Probe on in_1
  // Probe on in_2
  Divider #(.width(32)) divider_1 (.a(In_Div1), .b(In_Div2), .out(divider_1_out), .rem(out_4));  // open: upper
  // Probe on out_4
  Negator #(.width(32)) negator_1 (.in(in_1), .out(negator_1_out));
  Negator #(.width(32)) negator_2 (.in(in_2), .out(negator_2_out));
  xor xor_1 (xor_1_out, in_1[31], in_2[31]);
  Negator #(.width(32)) negator_3 (.in(divider_1_out), .out(negator_3_out));
  Multiplexer #(.width(32), .enable("false")) multiplexer_1 (
    .in0(in_1), .in1(negator_1_out), .out(In_Div1), .sel(in_1[31]));
  Multiplexer #(.width(32), .enable("false")) multiplexer_2 (
    .in0(in_2), .in1(negator_2_out), .out(In_Div2), .sel(in_2[31]));
  // Probe on out_3
  Multiplexer #(.width(32), .enable("false")) multiplexer_3 (
    .in0(divider_1_out), .in1(negator_3_out), .out(out_3), .sel(xor_1_out));

  // Other names for the same wires on the sheet: Carry_Out[31:0] = out_4; Input1[31:0] = in_1; Sign1 = in_1[31];
  //   Input2[31:0] = in_2; Sign2 = in_2[31]; Result[31:0] = out_3

  // Notes on the sheet:
  //   INPUT
  //   OUTPUT
  //   Part1
  //   Part2
  //   Separador
  //   Separador
endmodule

module Register_Bank (
  input  in_1,
  input  in_2,
  input  in_3,
  input  [4:0] in_4,
  input  [4:0] in_5,
  input  [4:0] in_6,
  input  [31:0] in_7,
  output [31:0] out_8,
  output [31:0] out_9,
  output [31:0] out_10
);

  wire Input_0, Input_1, Input_2, Input_3, Input_4, Input_5, Input_6, Input_7, Input_8, Input_9, Input_10,
       Input_11, Input_12, Input_13, Input_14, Input_15, Input_16, Input_17, Input_18, Input_19, Input_20,
       Input_21, Input_22, Input_23, Input_24, Input_25, Input_26, Input_27, Input_28, Input_29, Input_30,
       Input_31;
  wire [31:0] R0, R1, R2, R3, R4, R5, R6, R7, R8, R9, R10, R11, R12, R13, R14, R15, R16, R17, R18, R19, R20,
       R21, R22, R23, R24, R25, R26, R27, R28, R29, R30;

  Demultiplexer #(.select(5), .enable("false")) demultiplexer_1 (
    .out0(Input_0), .out1(Input_1), .out2(Input_2), .out3(Input_3), .out4(Input_4), .out5(Input_5),
    .out6(Input_6), .out7(Input_7), .out8(Input_8), .out9(Input_9), .out10(Input_10), .out11(Input_11),
    .out12(Input_12), .out13(Input_13), .out14(Input_14), .out15(Input_15), .out16(Input_16),
    .out17(Input_17), .out18(Input_18), .out19(Input_19), .out20(Input_20), .out21(Input_21),
    .out22(Input_22), .out23(Input_23), .out24(Input_24), .out25(Input_25), .out26(Input_26),
    .out27(Input_27), .out28(Input_28), .out29(Input_29), .out30(Input_30), .out31(Input_31), .in(in_3),
    .sel(in_6));
  Multiplexer #(.select(5), .width(32), .enable("false")) multiplexer_1 (
    .in0(R0), .in1(R1), .in2(R2), .in3(R3), .in4(R4), .in5(R5), .in6(R6), .in7(R7), .in8(R8), .in9(R9),
    .in10(R10), .in11(R11), .in12(R12), .in13(R13), .in14(R14), .in15(R15), .in16(R16), .in17(R17),
    .in18(R18), .in19(R19), .in20(R20), .in21(R21), .in22(R22), .in23(R23), .in24(R24), .in25(R25),
    .in26(R26), .in27(R27), .in28(R28), .in29(R29), .in30(R30), .in31(out_10), .out(out_8), .sel(in_4));
  Register #(.width(32)) u_R0 (.D({32{1'b0}}), .en(Input_0), .Q(R0), .clk(in_1), .clr(in_2));
  Register #(.width(32)) u_R1 (.D(in_7), .en(Input_1), .Q(R1), .clk(in_1), .clr(in_2));
  Register #(.width(32)) u_R2 (.D(in_7), .en(Input_2), .Q(R2), .clk(in_1), .clr(in_2));
  Register #(.width(32)) u_R3 (.D(in_7), .en(Input_3), .Q(R3), .clk(in_1), .clr(in_2));
  Register #(.width(32)) u_R4 (.D(in_7), .en(Input_4), .Q(R4), .clk(in_1), .clr(in_2));
  Register #(.width(32)) u_R5 (.D(in_7), .en(Input_5), .Q(R5), .clk(in_1), .clr(in_2));
  Register #(.width(32)) u_R6 (.D(in_7), .en(Input_6), .Q(R6), .clk(in_1), .clr(in_2));
  Register #(.width(32)) u_R7 (.D(in_7), .en(Input_7), .Q(R7), .clk(in_1), .clr(in_2));
  Register #(.width(32)) u_R8 (.D(in_7), .en(Input_8), .Q(R8), .clk(in_1), .clr(in_2));
  Register #(.width(32)) u_R9 (.D(in_7), .en(Input_9), .Q(R9), .clk(in_1), .clr(in_2));
  Register #(.width(32)) u_R10 (.D(in_7), .en(Input_10), .Q(R10), .clk(in_1), .clr(in_2));
  Register #(.width(32)) u_R11 (.D(in_7), .en(Input_11), .Q(R11), .clk(in_1), .clr(in_2));
  Register #(.width(32)) u_R12 (.D(in_7), .en(Input_12), .Q(R12), .clk(in_1), .clr(in_2));
  Register #(.width(32)) u_R13 (.D(in_7), .en(Input_13), .Q(R13), .clk(in_1), .clr(in_2));
  Register #(.width(32)) u_R14 (.D(in_7), .en(Input_14), .Q(R14), .clk(in_1), .clr(in_2));
  Register #(.width(32)) u_R15 (.D(in_7), .en(Input_15), .Q(R15), .clk(in_1), .clr(in_2));
  Multiplexer #(.select(5), .width(32), .enable("false")) multiplexer_2 (
    .in0(R0), .in1(R1), .in2(R2), .in3(R3), .in4(R4), .in5(R5), .in6(R6), .in7(R7), .in8(R8), .in9(R9),
    .in10(R10), .in11(R11), .in12(R12), .in13(R13), .in14(R14), .in15(R15), .in16(R16), .in17(R17),
    .in18(R18), .in19(R19), .in20(R20), .in21(R21), .in22(R22), .in23(R23), .in24(R24), .in25(R25),
    .in26(R26), .in27(R27), .in28(R28), .in29(R29), .in30(R30), .in31(out_10), .out(out_9), .sel(in_5));
  Register #(.width(32)) u_R16 (.D(in_7), .en(Input_16), .Q(R16), .clk(in_1), .clr(in_2));
  Register #(.width(32)) u_R17 (.D(in_7), .en(Input_17), .Q(R17), .clk(in_1), .clr(in_2));
  Register #(.width(32)) u_R18 (.D(in_7), .en(Input_18), .Q(R18), .clk(in_1), .clr(in_2));
  Register #(.width(32)) u_R19 (.D(in_7), .en(Input_19), .Q(R19), .clk(in_1), .clr(in_2));
  Register #(.width(32)) u_R20 (.D(in_7), .en(Input_20), .Q(R20), .clk(in_1), .clr(in_2));
  Register #(.width(32)) u_R21 (.D(in_7), .en(Input_21), .Q(R21), .clk(in_1), .clr(in_2));
  Register #(.width(32)) u_R22 (.D(in_7), .en(Input_22), .Q(R22), .clk(in_1), .clr(in_2));
  Register #(.width(32)) u_R23 (.D(in_7), .en(Input_23), .Q(R23), .clk(in_1), .clr(in_2));
  Register #(.width(32)) u_R24 (.D(in_7), .en(Input_24), .Q(R24), .clk(in_1), .clr(in_2));
  Register #(.width(32)) u_R25 (.D(in_7), .en(Input_25), .Q(R25), .clk(in_1), .clr(in_2));
  Register #(.width(32)) u_R26 (.D(in_7), .en(Input_26), .Q(R26), .clk(in_1), .clr(in_2));
  Register #(.width(32)) u_R27 (.D(in_7), .en(Input_27), .Q(R27), .clk(in_1), .clr(in_2));
  Register #(.width(32)) u_R28 (.D(in_7), .en(Input_28), .Q(R28), .clk(in_1), .clr(in_2));
  Register #(.width(32)) u_R29 (.D(in_7), .en(Input_29), .Q(R29), .clk(in_1), .clr(in_2));
  Register #(.width(32)) u_R30 (.D(in_7), .en(Input_30), .Q(R30), .clk(in_1), .clr(in_2));
  Register #(.width(32)) R31 (.D(in_7), .en(Input_31), .Q(out_10), .clk(in_1), .clr(in_2));

  // Other names for the same wires on the sheet: CLK = in_1; DATA[31:0] = in_7; Destination[4:0] = in_6;
  //   Output_1[31:0] = out_8; Output_2[31:0] = out_9; ReadWrite = in_3; Reset = in_2; Selector_1[4:0] = in_4;
  //   Selector_2[4:0] = in_5; R31[31:0] = out_10; SP[31:0] = out_10

  // Notes on the sheet:
  //   Inputs
  //   Outputs
  //   Registers
endmodule
